// Logisim project Toy-16.circ as structural Verilog: 77 circuits, main circuit notgate
module notgate (
  input  in_1,
  output out_2
);

  Transistor #(.\type ("n")) transistor_1 (.in(1'b0), .out(out_2), .gate(in_1));
  Pull_Resistor #(.pull(1)) pull_resistor_1 (.node(out_2));
endmodule

module orGate (
  input  in_1,
  input  in_2,
  output out_3
);

  wire pull_resistor_1_node;

  Pull_Resistor #(.pull(1)) pull_resistor_1 (.node(pull_resistor_1_node));
  Transistor #(.\type ("n")) transistor_1 (.in(1'b0), .out(pull_resistor_1_node), .gate(in_1));
  Transistor #(.\type ("n")) transistor_2 (.in(1'b0), .out(pull_resistor_1_node), .gate(in_2));
  Pull_Resistor #(.pull(1)) pull_resistor_2 (.node(out_3));
  Transistor #(.\type ("n")) transistor_3 (.in(1'b0), .out(out_3), .gate(pull_resistor_1_node));
endmodule

module and_gate (
  input  in_1,
  input  in_2,
  output out_3
);

  wire pull_resistor_1_node, transistor_2_out;

  Pull_Resistor #(.pull(1)) pull_resistor_1 (.node(pull_resistor_1_node));
  Transistor #(.\type ("n")) transistor_1 (.in(transistor_2_out), .out(pull_resistor_1_node), .gate(in_1));
  Transistor #(.\type ("n")) transistor_2 (.in(1'b0), .out(transistor_2_out), .gate(in_2));
  Pull_Resistor #(.pull(1)) pull_resistor_2 (.node(out_3));
  Transistor #(.\type ("n")) transistor_3 (.in(1'b0), .out(out_3), .gate(pull_resistor_1_node));
endmodule

module test (
  input  in_1,
  output [1:0] out_2
);


  assign out_2 = {2{in_1}};
endmodule

module assignment (
  input  in_1
);

  wire bcd_to_7_segment_decoder_3_p1, binary_to_bcd_converter_1_p2, binary_to_bcd_converter_1_p4, CLOCK,
       comparator_1_eq, comparator_2_eq, comparator_3_eq, comparator_4_eq, comparator_5_eq, j_k_ff_1_q,
       j_k_ff_2_q;
  wire [7:0] counter_1_q;

  Clock clock_1 (.out(CLOCK));
  Counter #(.max('h10)) counter_1 (.clr(in_1), .clk(CLOCK), .Q(counter_1_q));  // open: load, up, count, D, carry
  _7_Segment_Display u_7_segment_display_1 ();  // open: g, f, a, b, e, d, c, dp
  // BCD_to_7_Segment_decoder bcd_to_7_segment_decoder_1: pin names not known
  // Binary_to_BCD_converter #(.binvalue(8)) binary_to_bcd_converter_1: pin names not known; wires that end beside it: counter_1_q, binary_to_bcd_converter_1_p2, binary_to_bcd_converter_1_p2, binary_to_bcd_converter_1_p4
  Comparator comparator_1 (.a(8'h5), .b(counter_1_q), .eq(comparator_1_eq));  // open: gt, lt
  Comparator comparator_2 (.a(8'ha), .b(counter_1_q), .eq(comparator_2_eq));  // open: gt, lt
  _7_Segment_Display u_7_segment_display_2 ();  // open: g, f, a, b, e, d, c, dp
  // BCD_to_7_Segment_decoder bcd_to_7_segment_decoder_2: pin names not known; wires that end beside it: binary_to_bcd_converter_1_p4
  Comparator comparator_3 (.a({8{1'b0}}), .b(counter_1_q), .eq(comparator_3_eq));  // open: gt, lt
  Comparator comparator_4 (.a(8'h2), .b(counter_1_q), .eq(comparator_4_eq));  // open: gt, lt
  Comparator comparator_5 (.a(8'ha), .b(counter_1_q), .eq(comparator_5_eq));  // open: gt, lt
  J_K_Flip_Flop j_k_ff_1 (
    .J(comparator_1_eq), .K(comparator_2_eq), .clk(CLOCK), .Q(j_k_ff_1_q));  // open: Qn, preset, reset
  _7_Segment_Display u_7_segment_display_3 ();  // open: g, f, a, b, e, d, c, dp
  // BCD_to_7_Segment_decoder bcd_to_7_segment_decoder_3: pin names not known; wires that end beside it: bcd_to_7_segment_decoder_3_p1
  LED led_1 (.in(comparator_3_eq));
  J_K_Flip_Flop j_k_ff_2 (
    .J(comparator_4_eq), .K(comparator_5_eq), .clk(CLOCK), .Q(j_k_ff_2_q));  // open: Qn, preset, reset
  // Buzzer buzzer_1: pin names not known; wires that end beside it: bcd_to_7_segment_decoder_3_p1, 14'h533, comparator_3_eq
  // Buzzer buzzer_2: pin names not known; wires that end beside it: 14'h320, j_k_ff_2_q
  // Buzzer buzzer_3: pin names not known; wires that end beside it: 14'h42a, j_k_ff_1_q
  // Digital_Oscilloscope #(.nState(20)) digital_oscilloscope_1: pin names not known; wires that end beside it: CLOCK, comparator_3_eq, j_k_ff_2_q, j_k_ff_1_q
endmodule

module half_adder (
  input  A,
  input  B,
  output Sum,
  output Carry
);

  xor xor_1 (Sum, A, B);
  and and_1 (Carry, A, B);
endmodule

module full_adder (
  input  A,
  input  B,
  input  Cin,
  output Sum,
  output Cout
);

  odd odd_1 (.A(A), .B(B), .C(Cin), .O(Sum));
  maj maj_1 (.A(A), .B(B), .C(Cin), .O(Cout));
endmodule

module full_adder_4bit (
  input  A,
  input  B,
  input  Carry,
  input  A2,
  input  B2,
  input  A3,
  input  B3,
  input  A4,
  input  B4,
  output S1,
  output S2,
  output S3,
  output S4,
  output C
);

  wire full_adder_1_cout, full_adder_2_cout, full_adder_3_cout;

  full_adder full_adder_1 (.A(A), .B(B), .Cin(Carry), .Sum(S1), .Cout(full_adder_1_cout));
  full_adder full_adder_2 (.A(A2), .B(B2), .Cin(full_adder_1_cout), .Sum(S2), .Cout(full_adder_2_cout));
  full_adder full_adder_3 (.A(A3), .B(B3), .Cin(full_adder_2_cout), .Sum(S3), .Cout(full_adder_3_cout));
  full_adder full_adder_4 (.A(A4), .B(B4), .Cin(full_adder_3_cout), .Sum(S4), .Cout(C));
endmodule

module Multiplexer_2to1 (
  input  A,
  input  B,
  input  Selector,
  output OUT1
);

  wire and_1_out, and_2_out, not_1_out;

  and and_1 (and_1_out, B, not_1_out);
  not not_1 (not_1_out, Selector);
  and and_2 (and_2_out, A, Selector);
  or or_1 (OUT1, and_2_out, and_1_out);
endmodule

module Multiplexer_4to1 (
  input  A,
  input  B,
  input  A2,
  input  B2,
  input  Selector2,
  input  Selector1,
  output O1
);

  wire multiplexer_2to1_1_out1, multiplexer_2to1_2_out1;

  Multiplexer_2to1 multiplexer_2to1_1 (.A(A), .B(B), .Selector(Selector1), .OUT1(multiplexer_2to1_1_out1));
  Multiplexer_2to1 multiplexer_2to1_2 (.A(A2), .B(B2), .Selector(Selector1), .OUT1(multiplexer_2to1_2_out1));
  Multiplexer_2to1 multiplexer_2to1_3 (
    .A(multiplexer_2to1_1_out1), .B(multiplexer_2to1_2_out1), .Selector(Selector2), .OUT1(O1));
endmodule

module NOT_GATE (
  input  in_1,
  output out_2
);

  Pull_Resistor #(.pull(1)) pull_resistor_1 (.node(out_2));
  Transistor #(.\type ("n")) transistor_1 (.in(1'b0), .out(out_2), .gate(in_1));
endmodule

module NAND_GATE (
  input  in_1,
  input  in_2,
  output out_3
);

  wire transistor_2_out;

  Pull_Resistor #(.pull(1)) pull_resistor_1 (.node(out_3));
  Transistor #(.\type ("n")) transistor_1 (.in(transistor_2_out), .out(out_3), .gate(in_1));
  Transistor #(.\type ("n")) transistor_2 (.in(1'b0), .out(transistor_2_out), .gate(in_2));
endmodule

module NOR_GATE (
  input  in_1,
  input  in_2,
  output out_3
);

  Pull_Resistor #(.pull(1)) pull_resistor_1 (.node(out_3));
  Transistor #(.\type ("n")) transistor_1 (.in(1'b0), .out(out_3), .gate(in_1));
  Transistor #(.\type ("n")) transistor_2 (.in(1'b0), .out(out_3), .gate(in_2));
endmodule

module or_gate_design_2 (
  input  in_1,
  input  in_2,
  output out_3
);

  wire pull_resistor_1_node;

  Pull_Resistor #(.pull(1)) pull_resistor_1 (.node(pull_resistor_1_node));
  Transistor #(.\type ("n")) transistor_1 (.in(1'b0), .out(pull_resistor_1_node), .gate(in_1));
  Transistor #(.\type ("n")) transistor_2 (.in(1'b0), .out(pull_resistor_1_node), .gate(in_2));
  NOT_GATE not_gate_1 (.in_1(pull_resistor_1_node), .out_2(out_3));
endmodule

module and_gate_design_2 (
  input  in_1,
  input  in_2,
  output out_3
);

  wire pull_resistor_1_node, transistor_2_out;

  Pull_Resistor #(.pull(1)) pull_resistor_1 (.node(pull_resistor_1_node));
  Transistor #(.\type ("n")) transistor_1 (.in(transistor_2_out), .out(pull_resistor_1_node), .gate(in_1));
  Transistor #(.\type ("n")) transistor_2 (.in(1'b0), .out(transistor_2_out), .gate(in_2));
  NOT_GATE not_gate_1 (.in_1(pull_resistor_1_node), .out_2(out_3));
endmodule

module XOR_GATE (
  input  in_1,
  input  in_2,
  output out_3
);

  wire pull_resistor_2_node, transistor_2_out;

  Pull_Resistor #(.pull(1)) pull_resistor_1 (.node(out_3));
  Transistor #(.\type ("n")) transistor_1 (.in(transistor_2_out), .out(out_3), .gate(in_1));
  Transistor #(.\type ("n")) transistor_2 (.in(1'b0), .out(transistor_2_out), .gate(in_2));
  Pull_Resistor #(.pull(1)) pull_resistor_2 (.node(pull_resistor_2_node));
  Transistor #(.\type ("n")) transistor_3 (.in(1'b0), .out(pull_resistor_2_node), .gate(in_2));
  Transistor #(.\type ("n")) transistor_4 (.in(1'b0), .out(pull_resistor_2_node), .gate(in_1));
  Pull_Resistor #(.pull(1)) pull_resistor_3 (.node(out_3));
  Transistor #(.\type ("n")) transistor_5 (.in(1'b0), .out(out_3), .gate(pull_resistor_2_node));
endmodule

module XNOR_GATE (
  input  in_1,
  input  in_2,
  output out_3
);

  wire pull_resistor_1_node, pull_resistor_2_node, transistor_2_out;

  Pull_Resistor #(.pull(1)) pull_resistor_1 (.node(pull_resistor_1_node));
  Transistor #(.\type ("n")) transistor_1 (.in(transistor_2_out), .out(pull_resistor_1_node), .gate(in_1));
  Transistor #(.\type ("n")) transistor_2 (.in(1'b0), .out(transistor_2_out), .gate(in_2));
  Pull_Resistor #(.pull(1)) pull_resistor_2 (.node(pull_resistor_2_node));
  Transistor #(.\type ("n")) transistor_3 (.in(1'b0), .out(pull_resistor_2_node), .gate(in_2));
  Transistor #(.\type ("n")) transistor_4 (.in(1'b0), .out(pull_resistor_2_node), .gate(in_1));
  Pull_Resistor #(.pull(1)) pull_resistor_3 (.node(pull_resistor_1_node));
  Transistor #(.\type ("n")) transistor_5 (.in(1'b0), .out(pull_resistor_1_node), .gate(pull_resistor_2_node));
  Pull_Resistor #(.pull(1)) pull_resistor_4 (.node(out_3));
  Transistor #(.\type ("n")) transistor_6 (.in(1'b0), .out(out_3), .gate(pull_resistor_1_node));
endmodule

module Decoder_Custom (
  input  A2,
  input  A1,
  input  A0,
  input  EN,
  output out_5,
  output out_6,
  output out_7,
  output out_8,
  output out_9,
  output out_10,
  output out_11,
  output out_12
);

  wire not_1_out, not_2_out, not_3_out;

  not not_1 (not_1_out, A2);
  not not_2 (not_2_out, A1);
  not not_3 (not_3_out, A0);
  and and_1 (out_5, not_1_out, not_2_out, not_3_out, EN);
  and and_2 (out_6, A0, not_2_out, not_1_out, EN);
  and and_3 (out_7, not_3_out, A1, not_1_out, EN);
  and and_4 (out_8, A0, A1, not_1_out, EN);
  and and_5 (out_9, not_3_out, not_2_out, A2, EN);
  and and_6 (out_10, A0, not_2_out, A2, EN);
  and and_7 (out_11, not_3_out, A1, A2, EN);
  and and_8 (out_12, A0, A1, A2, EN);
endmodule

module and_gate_4 (
  input  in_1,
  input  in_2,
  input  in_3,
  input  in_4,
  output out_5
);

  wire pull_resistor_1_node, transistor_2_out, transistor_3_out, transistor_4_out;

  Pull_Resistor #(.pull(1)) pull_resistor_1 (.node(pull_resistor_1_node));
  Transistor #(.\type ("n")) transistor_1 (.in(transistor_2_out), .out(pull_resistor_1_node), .gate(in_1));
  Transistor #(.\type ("n")) transistor_2 (.in(transistor_3_out), .out(transistor_2_out), .gate(in_2));
  Transistor #(.\type ("n")) transistor_3 (.in(transistor_4_out), .out(transistor_3_out), .gate(in_3));
  Transistor #(.\type ("n")) transistor_4 (.in(1'b0), .out(transistor_4_out), .gate(in_4));
  NOT_GATE not_gate_1 (.in_1(pull_resistor_1_node), .out_2(out_5));
endmodule

module left_shift (
  input  [3:0] in_1,
  input  CIN,
  input  EN,
  output [3:0] out_4
);

  Multiplexer multiplexer_1 (.in0(in_1[3]), .in1(in_1[2]), .out(out_4[3]), .sel(EN));
  Multiplexer multiplexer_2 (.in0(in_1[2]), .in1(in_1[1]), .out(out_4[2]), .sel(EN));
  Multiplexer multiplexer_3 (.in0(in_1[1]), .in1(in_1[0]), .out(out_4[1]), .sel(EN));
  Multiplexer multiplexer_4 (.in0(in_1[0]), .in1(CIN), .out(out_4[0]), .sel(EN));
endmodule

module decoder_and_demux (
  input  input1,
  input  A2,
  input  A1,
  input  A0,
  output out_5,
  output out_6,
  output out_7,
  output out_8,
  output out_9,
  output out_10,
  output out_11,
  output out_12,
  output out_13,
  output out_14,
  output out_15,
  output out_16,
  output out_17,
  output out_18,
  output out_19,
  output out_20
);

  wire not_1_out, not_2_out, not_3_out;

  not not_1 (not_1_out, A2);
  not not_2 (not_2_out, A1);
  not not_3 (not_3_out, A0);
  and and_1 (out_6, not_1_out, not_2_out, not_3_out);
  and and_2 (out_8, A0, not_2_out, not_1_out);
  and and_3 (out_10, not_3_out, A1, not_1_out);
  and and_4 (out_12, A0, A1, not_1_out);
  and and_5 (out_14, not_3_out, not_2_out, A2);
  and and_6 (out_17, A0, not_2_out, A2);
  and and_7 (out_19, not_3_out, A1, A2);
  and and_8 (out_20, A0, A1, A2);
  and and_9 (out_5, out_6, input1);
  and and_10 (out_7, out_8, input1);
  and and_11 (out_9, out_10, input1);
  and and_12 (out_11, out_12, input1);
  and and_13 (out_13, out_14, input1);
  and and_14 (out_15, out_17, input1);
  and and_15 (out_16, out_19, input1);
  and and_16 (out_18, out_20, input1);
endmodule

module ALU (
  input  [7:0] A,
  input  [7:0] B,
  input  ADD,
  input  AND1,
  input  XOR1,
  output [7:0] OUT1
);

  wire [7:0] and_1_out, and_2_out, and_3_out, and_gate_8bit_1_out_3, full_adder_8bit_1_s1,
       xor_gate_8bit_1_out_3;

  full_adder_8bit full_adder_8bit_1 (
    .A(A[0]), .B(B[0]), .Carry(1'b0), .A2(A[1]), .B2(B[1]), .A3(A[2]), .B3(B[2]), .A4(A[3]), .B4(B[3]),
    .A5(A[4]), .B5(B[4]), .A6(A[5]), .B6(B[5]), .A7(A[6]), .B7(B[6]), .A8(A[7]), .B8(B[7]),
    .S1(full_adder_8bit_1_s1[0]), .S2(full_adder_8bit_1_s1[1]), .S3(full_adder_8bit_1_s1[2]),
    .S4(full_adder_8bit_1_s1[3]), .S5(full_adder_8bit_1_s1[4]), .S6(full_adder_8bit_1_s1[5]),
    .S7(full_adder_8bit_1_s1[6]), .S8(full_adder_8bit_1_s1[7]));  // open: C
  and_gate_8bit and_gate_8bit_1 (.in_1(A), .in_2(B), .out_3(and_gate_8bit_1_out_3));
  XOR_GATE_8bit xor_gate_8bit_1 (.in_1(A), .in_2(B), .out_3(xor_gate_8bit_1_out_3));
  assign and_1_out = full_adder_8bit_1_s1 & {8{ADD}};  // AND_Gate and_1, 8 bits wide
  assign and_2_out = and_gate_8bit_1_out_3 & {8{AND1}};  // AND_Gate and_2, 8 bits wide
  assign and_3_out = xor_gate_8bit_1_out_3 & {8{XOR1}};  // AND_Gate and_3, 8 bits wide
  assign OUT1 = and_1_out | and_2_out | and_3_out;  // OR_Gate or_1, 8 bits wide
endmodule

module full_adder_8bit (
  input  A,
  input  B,
  input  Carry,
  input  A2,
  input  B2,
  input  A3,
  input  B3,
  input  A4,
  input  B4,
  input  A5,
  input  B5,
  input  A6,
  input  B6,
  input  A7,
  input  B7,
  input  A8,
  input  B8,
  output S1,
  output S2,
  output S3,
  output S4,
  output S5,
  output S6,
  output S7,
  output S8,
  output C
);

  wire full_adder_1_cout, full_adder_2_cout, full_adder_3_cout, full_adder_4_cout, full_adder_5_cout,
       full_adder_6_cout, full_adder_7_cout;

  full_adder full_adder_1 (.A(A), .B(B), .Cin(Carry), .Sum(S1), .Cout(full_adder_1_cout));
  full_adder full_adder_2 (.A(A2), .B(B2), .Cin(full_adder_1_cout), .Sum(S2), .Cout(full_adder_2_cout));
  full_adder full_adder_3 (.A(A3), .B(B3), .Cin(full_adder_2_cout), .Sum(S3), .Cout(full_adder_3_cout));
  full_adder full_adder_4 (.A(A4), .B(B4), .Cin(full_adder_3_cout), .Sum(S4), .Cout(full_adder_4_cout));
  full_adder full_adder_5 (.A(A5), .B(B5), .Cin(full_adder_4_cout), .Sum(S5), .Cout(full_adder_5_cout));
  full_adder full_adder_6 (.A(A6), .B(B6), .Cin(full_adder_5_cout), .Sum(S6), .Cout(full_adder_6_cout));
  full_adder full_adder_7 (.A(A7), .B(B7), .Cin(full_adder_6_cout), .Sum(S7), .Cout(full_adder_7_cout));
  full_adder full_adder_8 (.A(A8), .B(B8), .Cin(full_adder_7_cout), .Sum(S8), .Cout(C));
endmodule

module and_gate_8bit (
  input  [7:0] in_1,
  input  [7:0] in_2,
  output [7:0] out_3
);

  and_gate_design_2 and_gate_design_2_1 (.in_1(in_1[0]), .in_2(in_2[0]), .out_3(out_3[0]));
  and_gate_design_2 and_gate_design_2_2 (.in_1(in_1[1]), .in_2(in_2[1]), .out_3(out_3[1]));
  and_gate_design_2 and_gate_design_2_3 (.in_1(in_1[2]), .in_2(in_2[2]), .out_3(out_3[2]));
  and_gate_design_2 and_gate_design_2_4 (.in_1(in_1[3]), .in_2(in_2[3]), .out_3(out_3[3]));
  and_gate_design_2 and_gate_design_2_5 (.in_1(in_1[4]), .in_2(in_2[4]), .out_3(out_3[4]));
  and_gate_design_2 and_gate_design_2_6 (.in_1(in_1[5]), .in_2(in_2[5]), .out_3(out_3[5]));
  and_gate_design_2 and_gate_design_2_7 (.in_1(in_1[6]), .in_2(in_2[6]), .out_3(out_3[6]));
  and_gate_design_2 and_gate_design_2_8 (.in_1(in_1[7]), .in_2(in_2[7]), .out_3(out_3[7]));
endmodule

module XOR_GATE_8bit (
  input  [7:0] in_1,
  input  [7:0] in_2,
  output [7:0] out_3
);

  XOR_GATE xor_gate_1 (.in_1(in_1[0]), .in_2(in_2[0]), .out_3(out_3[0]));
  XOR_GATE xor_gate_2 (.in_1(in_1[1]), .in_2(in_2[1]), .out_3(out_3[1]));
  XOR_GATE xor_gate_3 (.in_1(in_1[2]), .in_2(in_2[2]), .out_3(out_3[2]));
  XOR_GATE xor_gate_4 (.in_1(in_1[3]), .in_2(in_2[3]), .out_3(out_3[3]));
  XOR_GATE xor_gate_5 (.in_1(in_1[4]), .in_2(in_2[4]), .out_3(out_3[4]));
  XOR_GATE xor_gate_6 (.in_1(in_1[5]), .in_2(in_2[5]), .out_3(out_3[5]));
  XOR_GATE xor_gate_7 (.in_1(in_1[6]), .in_2(in_2[6]), .out_3(out_3[6]));
  XOR_GATE xor_gate_8 (.in_1(in_1[7]), .in_2(in_2[7]), .out_3(out_3[7]));
endmodule

module full_adder_8 (
  input  CIN,
  input  [7:0] A,
  input  [7:0] B,
  output [7:0] OUT1
);

  wire full_adder_1_cout, full_adder_2_cout, full_adder_3_cout, full_adder_4_cout, full_adder_5_cout,
       full_adder_6_cout, full_adder_7_cout;

  full_adder full_adder_1 (.A(A[0]), .B(B[0]), .Cin(CIN), .Sum(OUT1[0]), .Cout(full_adder_1_cout));
  full_adder full_adder_2 (.A(A[1]), .B(B[1]), .Cin(full_adder_1_cout), .Sum(OUT1[1]), .Cout(full_adder_2_cout));
  full_adder full_adder_3 (.A(A[2]), .B(B[2]), .Cin(full_adder_2_cout), .Sum(OUT1[2]), .Cout(full_adder_3_cout));
  full_adder full_adder_4 (.A(A[3]), .B(B[3]), .Cin(full_adder_3_cout), .Sum(OUT1[3]), .Cout(full_adder_4_cout));
  full_adder full_adder_5 (.A(A[4]), .B(B[4]), .Cin(full_adder_4_cout), .Sum(OUT1[4]), .Cout(full_adder_5_cout));
  full_adder full_adder_6 (.A(A[5]), .B(B[5]), .Cin(full_adder_5_cout), .Sum(OUT1[5]), .Cout(full_adder_6_cout));
  full_adder full_adder_7 (.A(A[6]), .B(B[6]), .Cin(full_adder_6_cout), .Sum(OUT1[6]), .Cout(full_adder_7_cout));
  full_adder full_adder_8 (.A(A[7]), .B(B[7]), .Cin(full_adder_7_cout), .Sum(OUT1[7]));  // open: Cout
endmodule

module ALU_2 (
  input  [7:0] A,
  input  [7:0] B,
  input  ADD,
  input  AND1,
  input  XOR1,
  output [7:0] OUT1
);

  wire [7:0] and_1_out, and_2_out, and_3_out, and_gate_8bit_1_out_3, full_adder_8_1_out1,
       xor_gate_8bit_1_out_3;

  full_adder_8 full_adder_8_1 (.A(A), .B(B), .OUT1(full_adder_8_1_out1));  // open: CIN
  and_gate_8bit and_gate_8bit_1 (.in_1(A), .in_2(B), .out_3(and_gate_8bit_1_out_3));
  XOR_GATE_8bit xor_gate_8bit_1 (.in_1(A), .in_2(B), .out_3(xor_gate_8bit_1_out_3));
  assign and_1_out = full_adder_8_1_out1 & {8{ADD}};  // AND_Gate and_1, 8 bits wide
  assign and_2_out = and_gate_8bit_1_out_3 & {8{AND1}};  // AND_Gate and_2, 8 bits wide
  assign and_3_out = xor_gate_8bit_1_out_3 & {8{XOR1}};  // AND_Gate and_3, 8 bits wide
  assign OUT1 = and_1_out | and_2_out | and_3_out;  // OR_Gate or_1, 8 bits wide
endmodule

module left_shift_8bit (
  input  [7:0] in_1,
  input  CIN,
  input  EN,
  output [7:0] out_4
);

  Multiplexer multiplexer_1 (.in0(in_1[7]), .in1(in_1[6]), .out(out_4[7]), .sel(EN));
  Multiplexer multiplexer_2 (.in0(in_1[6]), .in1(in_1[5]), .out(out_4[6]), .sel(EN));
  Multiplexer multiplexer_3 (.in0(in_1[5]), .in1(in_1[4]), .out(out_4[5]), .sel(EN));
  Multiplexer multiplexer_4 (.in0(in_1[4]), .in1(in_1[3]), .out(out_4[4]), .sel(EN));
  Multiplexer multiplexer_5 (.in0(in_1[3]), .in1(in_1[2]), .out(out_4[3]), .sel(EN));
  Multiplexer multiplexer_6 (.in0(in_1[2]), .in1(in_1[1]), .out(out_4[2]), .sel(EN));
  Multiplexer multiplexer_7 (.in0(in_1[1]), .in1(in_1[0]), .out(out_4[1]), .sel(EN));
  Multiplexer multiplexer_8 (.in0(in_1[0]), .in1(CIN), .out(out_4[0]), .sel(EN));
endmodule

module right_shift_8bit (
  input  [7:0] in_1,
  input  EN,
  output [7:0] out_3
);

  Multiplexer multiplexer_1 (.in0(in_1[7]), .in1(1'b0), .out(out_3[7]), .sel(EN));
  Multiplexer multiplexer_2 (.in0(in_1[6]), .in1(in_1[7]), .out(out_3[6]), .sel(EN));
  Multiplexer multiplexer_3 (.in0(in_1[5]), .in1(in_1[6]), .out(out_3[5]), .sel(EN));
  Multiplexer multiplexer_4 (.in0(in_1[4]), .in1(in_1[5]), .out(out_3[4]), .sel(EN));
  Multiplexer multiplexer_5 (.in0(in_1[3]), .in1(in_1[4]), .out(out_3[3]), .sel(EN));
  Multiplexer multiplexer_6 (.in0(in_1[2]), .in1(in_1[3]), .out(out_3[2]), .sel(EN));
  Multiplexer multiplexer_7 (.in0(in_1[1]), .in1(in_1[2]), .out(out_3[1]), .sel(EN));
  Multiplexer multiplexer_8 (.in0(in_1[0]), .in1(in_1[1]), .out(out_3[0]), .sel(EN));
endmodule

module try_run (
  input  [7:0] in_1,
  input  [7:0] in_2,
  output [7:0] out_3
);

  full_adder_8 full_adder_8_1 (.CIN(in_1[0]), .A(in_2), .B(in_2), .OUT1(out_3));
  // Pins of 1 and 8 bits meet at in_1
endmodule

module SUB_8bit (
  input  [7:0] A,
  input  [7:0] B,
  input  SUB,
  output [7:0] out_4
);

  wire [7:0] xor_1_out;

  assign xor_1_out = {8{SUB}} ^ B;  // XOR_Gate xor_1, 8 bits wide
  full_adder_8 full_adder_8_1 (.CIN(SUB), .A(A), .B(xor_1_out), .OUT1(out_4));
endmodule

module or_gate_4 (
  input  in_1,
  input  in_2,
  input  in_3,
  input  in_4,
  input  in_5,
  input  in_6,
  output out_7
);

  wire pull_resistor_1_node;

  Pull_Resistor #(.pull(1)) pull_resistor_1 (.node(pull_resistor_1_node));
  Transistor #(.\type ("n")) transistor_1 (.in(1'b0), .out(pull_resistor_1_node), .gate(in_1));
  Transistor #(.\type ("n")) transistor_2 (.in(1'b0), .out(pull_resistor_1_node), .gate(in_2));
  Transistor #(.\type ("n")) transistor_3 (.in(1'b0), .out(pull_resistor_1_node), .gate(in_3));
  Transistor #(.\type ("n")) transistor_4 (.in(1'b0), .out(pull_resistor_1_node), .gate(in_4));
  Transistor #(.\type ("n")) transistor_5 (.in(1'b0), .out(pull_resistor_1_node), .gate(in_5));
  Transistor #(.\type ("n")) transistor_6 (.in(1'b0), .out(pull_resistor_1_node), .gate(in_6));
  Transistor #(.\type ("n")) transistor_7 (.in(1'b0), .out(out_7), .gate(pull_resistor_1_node));
  Pull_Resistor #(.pull(1)) pull_resistor_2 (.node(out_7));
endmodule

module ALU_final (
  input  [7:0] A,
  input  [7:0] B,
  input  ADD,
  input  AND1,
  input  XOR1,
  input  SUB,
  input  LSHIFT,
  input  RSHIFT,
  output [7:0] OUT1
);

  wire [7:0] and_1_out, and_2_out, and_3_out, and_4_out, and_5_out, and_6_out, and_gate_8bit_1_out_3,
       full_adder_8_1_out1, left_shift_8bit_1_out_4, right_shift_8bit_1_out_3, sub_8bit_1_out_4,
       xor_gate_8bit_1_out_3;

  SUB_8bit sub_8bit_1 (.A(A), .B(B), .SUB(SUB), .out_4(sub_8bit_1_out_4));
  left_shift_8bit left_shift_8bit_1 (.in_1(A), .CIN(1'b0), .EN(LSHIFT), .out_4(left_shift_8bit_1_out_4));
  right_shift_8bit right_shift_8bit_1 (.in_1(A), .EN(RSHIFT), .out_3(right_shift_8bit_1_out_3));
  full_adder_8 full_adder_8_1 (.A(A), .B(B), .OUT1(full_adder_8_1_out1));  // open: CIN
  and_gate_8bit and_gate_8bit_1 (.in_1(A), .in_2(B), .out_3(and_gate_8bit_1_out_3));
  XOR_GATE_8bit xor_gate_8bit_1 (.in_1(A), .in_2(B), .out_3(xor_gate_8bit_1_out_3));
  assign and_1_out = full_adder_8_1_out1 & {8{ADD}};  // AND_Gate and_1, 8 bits wide
  assign and_2_out = and_gate_8bit_1_out_3 & {8{AND1}};  // AND_Gate and_2, 8 bits wide
  assign and_3_out = xor_gate_8bit_1_out_3 & {8{XOR1}};  // AND_Gate and_3, 8 bits wide
  assign and_4_out = sub_8bit_1_out_4 & {8{SUB}};  // AND_Gate and_4, 8 bits wide
  assign and_5_out = left_shift_8bit_1_out_4 & {8{LSHIFT}};  // AND_Gate and_5, 8 bits wide
  assign and_6_out = right_shift_8bit_1_out_3 & {8{RSHIFT}};  // AND_Gate and_6, 8 bits wide
  assign OUT1 = and_5_out | and_1_out | and_4_out | and_2_out | and_3_out | and_6_out;  // OR_Gate or_1, 8 bits wide
endmodule

module MemoryBit (
  input  INPUT1,
  input  Write,
  output OUTPUT1
);

  wire and_1_out, and_2_out, nor_1_out, not_1_out;

  not not_1 (not_1_out, INPUT1);
  and and_1 (and_1_out, Write, INPUT1);
  and and_2 (and_2_out, Write, not_1_out);
  nor nor_1 (nor_1_out, and_1_out, OUTPUT1);
  nor nor_2 (OUTPUT1, nor_1_out, and_2_out);
endmodule

module Step_17 (
  output Fetch_Write,
  output Execute_Write,
  output Fetch,
  output Execute
);

  wire clock_1_out;

  Clock clock_1 (.out(clock_1_out));
  Custom_Flip_Flop custom_flip_flop_1 (.Data(Execute), .Clock_In(clock_1_out), .Q(Fetch), .Not_Q(Execute));
  and and_1 (Fetch_Write, Fetch, clock_1_out);
  and and_2 (Execute_Write, Execute, clock_1_out);
endmodule

module Custom_Flip_Flop (
  input  Data,
  input  Clock_In,
  output Q,
  output Not_Q
);

  wire memorybit_1_output1, not_1_out;

  not not_1 (not_1_out, Clock_In);
  MemoryBit memorybit_1 (.INPUT1(Data), .Write(Clock_In), .OUTPUT1(memorybit_1_output1));
  MemoryBit memorybit_2 (.INPUT1(memorybit_1_output1), .Write(not_1_out), .OUTPUT1(Q));
  not not_2 (Not_Q, Q);
endmodule

module Register_8bit (
  input  Write,
  input  [7:0] Data_In,
  output [7:0] Data_Out
);

  D_Flip_Flop d_ff_1 (.D(Data_In[0]), .clk(Write), .Q(Data_Out[0]));  // open: Qn, preset, reset
  D_Flip_Flop d_ff_2 (.D(Data_In[1]), .clk(Write), .Q(Data_Out[1]));  // open: Qn, preset, reset
  D_Flip_Flop d_ff_3 (.D(Data_In[2]), .clk(Write), .Q(Data_Out[2]));  // open: Qn, preset, reset
  D_Flip_Flop d_ff_4 (.D(Data_In[3]), .clk(Write), .Q(Data_Out[3]));  // open: Qn, preset, reset
  D_Flip_Flop d_ff_5 (.D(Data_In[4]), .clk(Write), .Q(Data_Out[4]));  // open: Qn, preset, reset
  D_Flip_Flop d_ff_6 (.D(Data_In[5]), .clk(Write), .Q(Data_Out[5]));  // open: Qn, preset, reset
  D_Flip_Flop d_ff_7 (.D(Data_In[6]), .clk(Write), .Q(Data_Out[6]));  // open: Qn, preset, reset
  D_Flip_Flop d_ff_8 (.D(Data_In[7]), .clk(Write), .Q(Data_Out[7]));  // open: Qn, preset, reset
endmodule

module Register_4bit (
  input  [3:0] Data_in,
  input  Write,
  output [3:0] Data_out
);

  D_Flip_Flop d_ff_1 (.D(Data_in[1]), .clk(Write), .Q(Data_out[1]));  // open: Qn, preset, reset
  D_Flip_Flop d_ff_2 (.D(Data_in[2]), .clk(Write), .Q(Data_out[2]));  // open: Qn, preset, reset
  D_Flip_Flop d_ff_3 (.D(Data_in[3]), .clk(Write), .Q(Data_out[3]));  // open: Qn, preset, reset
  D_Flip_Flop d_ff_4 (.D(Data_in[0]), .clk(Write), .Q(Data_out[0]));  // open: Qn, preset, reset
endmodule

module Memory_Bank_16x8 (
  input  [7:0] Input_Bus,
  input  [3:0] addr,
  input  Write,
  output [7:0] Output_bus
);

  wire decoder_1_out0, decoder_1_out1, decoder_1_out2, decoder_1_out3, decoder_1_out4, decoder_1_out5,
       decoder_1_out6, decoder_1_out7, decoder_1_out8, decoder_1_out9, decoder_1_out10, decoder_1_out11,
       decoder_1_out12, decoder_1_out13, decoder_1_out14, decoder_1_out15;
  wire [7:0] register_8bit_1_data_out, register_8bit_2_data_out, register_8bit_3_data_out,
       register_8bit_4_data_out, register_8bit_5_data_out, register_8bit_6_data_out,
       register_8bit_7_data_out, register_8bit_8_data_out, register_8bit_9_data_out,
       register_8bit_10_data_out, register_8bit_11_data_out, register_8bit_12_data_out,
       register_8bit_13_data_out, register_8bit_14_data_out, register_8bit_15_data_out,
       register_8bit_16_data_out;

  Decoder #(.select(4)) decoder_1 (
    .out0(decoder_1_out0), .out1(decoder_1_out1), .out2(decoder_1_out2), .out3(decoder_1_out3),
    .out4(decoder_1_out4), .out5(decoder_1_out5), .out6(decoder_1_out6), .out7(decoder_1_out7),
    .out8(decoder_1_out8), .out9(decoder_1_out9), .out10(decoder_1_out10), .out11(decoder_1_out11),
    .out12(decoder_1_out12), .out13(decoder_1_out13), .out14(decoder_1_out14), .out15(decoder_1_out15),
    .sel(addr), .en(Write));
  Register_8bit register_8bit_1 (.Write(decoder_1_out0), .Data_In(Input_Bus), .Data_Out(register_8bit_1_data_out));
  Register_8bit register_8bit_2 (.Write(decoder_1_out1), .Data_In(Input_Bus), .Data_Out(register_8bit_2_data_out));
  Register_8bit register_8bit_3 (.Write(decoder_1_out2), .Data_In(Input_Bus), .Data_Out(register_8bit_3_data_out));
  Register_8bit register_8bit_4 (.Write(decoder_1_out3), .Data_In(Input_Bus), .Data_Out(register_8bit_4_data_out));
  Register_8bit register_8bit_5 (.Write(decoder_1_out4), .Data_In(Input_Bus), .Data_Out(register_8bit_5_data_out));
  Register_8bit register_8bit_6 (.Write(decoder_1_out5), .Data_In(Input_Bus), .Data_Out(register_8bit_6_data_out));
  Register_8bit register_8bit_7 (.Write(decoder_1_out6), .Data_In(Input_Bus), .Data_Out(register_8bit_7_data_out));
  Register_8bit register_8bit_8 (.Write(decoder_1_out7), .Data_In(Input_Bus), .Data_Out(register_8bit_8_data_out));
  Register_8bit register_8bit_9 (.Write(decoder_1_out8), .Data_In(Input_Bus), .Data_Out(register_8bit_9_data_out));
  Register_8bit register_8bit_10 (.Write(decoder_1_out9), .Data_In(Input_Bus), .Data_Out(register_8bit_10_data_out));
  Register_8bit register_8bit_11 (.Write(decoder_1_out10), .Data_In(Input_Bus), .Data_Out(register_8bit_11_data_out));
  Register_8bit register_8bit_12 (.Write(decoder_1_out11), .Data_In(Input_Bus), .Data_Out(register_8bit_12_data_out));
  Register_8bit register_8bit_13 (.Write(decoder_1_out12), .Data_In(Input_Bus), .Data_Out(register_8bit_13_data_out));
  Register_8bit register_8bit_14 (.Write(decoder_1_out13), .Data_In(Input_Bus), .Data_Out(register_8bit_14_data_out));
  Register_8bit register_8bit_15 (.Write(decoder_1_out14), .Data_In(Input_Bus), .Data_Out(register_8bit_15_data_out));
  Register_8bit register_8bit_16 (.Write(decoder_1_out15), .Data_In(Input_Bus), .Data_Out(register_8bit_16_data_out));
  Mux16_to_1 mux16_to_1_1 (
    .in_1(register_8bit_1_data_out), .in_2(register_8bit_2_data_out), .in_3(register_8bit_3_data_out),
    .in_4(register_8bit_4_data_out), .in_5(register_8bit_5_data_out), .in_6(register_8bit_6_data_out),
    .in_7(register_8bit_7_data_out), .in_8(register_8bit_8_data_out), .in_9(register_8bit_9_data_out),
    .in_10(register_8bit_10_data_out), .in_11(register_8bit_11_data_out), .in_12(register_8bit_12_data_out),
    .in_13(register_8bit_13_data_out), .in_14(register_8bit_14_data_out), .in_15(register_8bit_15_data_out),
    .in_16(register_8bit_16_data_out), .Sel(addr), .OUT1(Output_bus));
endmodule

module Mux16_to_1 (
  input  [7:0] in_1,
  input  [7:0] in_2,
  input  [7:0] in_3,
  input  [7:0] in_4,
  input  [7:0] in_5,
  input  [7:0] in_6,
  input  [7:0] in_7,
  input  [7:0] in_8,
  input  [7:0] in_9,
  input  [7:0] in_10,
  input  [7:0] in_11,
  input  [7:0] in_12,
  input  [7:0] in_13,
  input  [7:0] in_14,
  input  [7:0] in_15,
  input  [7:0] in_16,
  input  [3:0] Sel,
  output [7:0] OUT1
);

  wire [7:0] mux_8bit_4to1_1_o1, mux_8bit_4to1_2_o1, mux_8bit_4to1_3_o1, mux_8bit_4to1_4_o1;

  Mux_8bit_4to1 mux_8bit_4to1_1 (
    .A(in_1), .B(in_2), .A2(in_3), .B2(in_4), .Selector2(Sel[1]), .Selector1(Sel[0]), .O1(mux_8bit_4to1_1_o1));
  Mux_8bit_4to1 mux_8bit_4to1_2 (
    .A(in_5), .B(in_6), .A2(in_7), .B2(in_8), .Selector2(Sel[1]), .Selector1(Sel[0]), .O1(mux_8bit_4to1_2_o1));
  Mux_8bit_4to1 mux_8bit_4to1_3 (
    .A(in_9), .B(in_10), .A2(in_11), .B2(in_12), .Selector2(Sel[1]), .Selector1(Sel[0]),
    .O1(mux_8bit_4to1_3_o1));
  Mux_8bit_4to1 mux_8bit_4to1_4 (
    .A(in_13), .B(in_14), .A2(in_15), .B2(in_16), .Selector2(Sel[1]), .Selector1(Sel[0]),
    .O1(mux_8bit_4to1_4_o1));
  Mux_8bit_4to1 mux_8bit_4to1_5 (
    .A(mux_8bit_4to1_1_o1), .B(mux_8bit_4to1_2_o1), .A2(mux_8bit_4to1_3_o1), .B2(mux_8bit_4to1_4_o1),
    .Selector2(Sel[3]), .Selector1(Sel[2]), .O1(OUT1));
endmodule

module Mux_8bit_2to1 (
  input  [7:0] A,
  input  [7:0] B,
  input  Selector,
  output [7:0] OUT1
);

  wire [7:0] and_1_out, and_2_out, not_1_out;

  assign not_1_out = ~{8{Selector}};  // NOT_Gate not_1, 8 bits wide
  assign and_1_out = B & {8{Selector}};  // AND_Gate and_1, 8 bits wide
  assign and_2_out = A & not_1_out;  // AND_Gate and_2, 8 bits wide
  assign OUT1 = and_2_out | and_1_out;  // OR_Gate or_1, 8 bits wide
endmodule

module Mux_8bit_4to1 (
  input  [7:0] A,
  input  [7:0] B,
  input  [7:0] A2,
  input  [7:0] B2,
  input  Selector2,
  input  Selector1,
  output [7:0] O1
);

  wire [7:0] mux_8bit_2to1_1_out1, mux_8bit_2to1_2_out1;

  Mux_8bit_2to1 mux_8bit_2to1_1 (.A(A), .B(B), .Selector(Selector1), .OUT1(mux_8bit_2to1_1_out1));
  Mux_8bit_2to1 mux_8bit_2to1_2 (.A(A2), .B(B2), .Selector(Selector1), .OUT1(mux_8bit_2to1_2_out1));
  Mux_8bit_2to1 mux_8bit_2to1_3 (.A(mux_8bit_2to1_1_out1), .B(mux_8bit_2to1_2_out1), .Selector(Selector2), .OUT1(O1));
endmodule

module Decoder_4to16 (
  input  [3:0] addr,
  input  Write,
  output OUT1,
  output out_4,
  output out_5,
  output out_6,
  output out_7,
  output out_8,
  output out_9,
  output out_10,
  output out_11,
  output out_12,
  output out_13,
  output out_14,
  output out_15,
  output out_16,
  output out_17,
  output out_18
);

  wire and_1_out, and_2_out, not_1_out;

  not not_1 (not_1_out, addr[2]);
  and and_1 (and_1_out, Write, addr[2]);
  and and_2 (and_2_out, not_1_out, Write);
  Decoder_Custom decoder_custom_1 (
    .A2(addr[0]), .A1(addr[1]), .A0(addr[2]), .EN(and_2_out), .out_5(OUT1), .out_6(out_4), .out_7(out_5),
    .out_8(out_6), .out_9(out_7), .out_10(out_8), .out_11(out_9), .out_12(out_10));
  Decoder_Custom decoder_custom_2 (
    .A2(addr[0]), .A1(addr[1]), .A0(addr[2]), .EN(and_1_out), .out_5(out_11), .out_6(out_12), .out_7(out_13),
    .out_8(out_14), .out_9(out_15), .out_10(out_16), .out_11(out_17), .out_12(out_18));
endmodule

module incrementer_4bit (
  input  [3:0] X,
  output [3:0] x_inc
);

  wire and_1_out, and_2_out, and_3_out;

  and and_1 (and_1_out, X[0], 1'b1);
  and and_2 (and_2_out, X[1], and_1_out);
  and and_3 (and_3_out, X[2], and_2_out);
  // AND_Gate and_4 has open pins: in0=X[3], in1=and_3_out, out=open
  xor xor_1 (x_inc[0], X[0], 1'b1);
  xor xor_2 (x_inc[1], X[1], and_1_out);
  xor xor_3 (x_inc[2], X[2], and_2_out);
  xor xor_4 (x_inc[3], X[3], and_3_out);
endmodule

module mux_2way (
  input  [3:0] Bus0,
  input  [3:0] InputBus,
  input  Sel,
  output [3:0] out_4
);

  wire not_1_out;

  not not_1 (not_1_out, Sel);
  assign out_4 = not_1_out ? Bus0 : 4'bz;  // Controlled_Buffer controlled_buffer_1
  assign out_4 = Sel ? InputBus : 4'bz;  // Controlled_Buffer controlled_buffer_2
endmodule

module Program_Counter (
  input  [3:0] InputBus,
  input  LOAD,
  input  WRITE,
  output [3:0] OutputBus
);

  wire [3:0] incrementer_4bit_1_x_inc, mux_2way_1_out_4;

  Register #(.width(4)) register_1 (.D(mux_2way_1_out_4), .clk(WRITE), .Q(OutputBus));  // open: en, clr
  incrementer_4bit incrementer_4bit_1 (.X(OutputBus), .x_inc(incrementer_4bit_1_x_inc));
  mux_2way mux_2way_1 (.Bus0(incrementer_4bit_1_x_inc), .InputBus(InputBus), .Sel(LOAD), .out_4(mux_2way_1_out_4));
endmodule

module Control_Unit (
  input  [3:0] opcode,
  input  Fetch,
  input  Fetch_Write,
  input  Execute,
  input  Execute_WRITE,
  input  [7:0] R,
  output HALT,
  output ALU_ADD,
  output ALU_XOR,
  output ALU_AND,
  output Memory_WRITE,
  output R_MUX_ALU,
  output R_MUX_MEMORY,
  output R_MUX_IR,
  output R_WRITE,
  output PC_INCREMENT,
  output PC_LOAD,
  output PC_WRITE,
  output ADDR_MUX_PC,
  output ADDR_MUX_IR,
  output IR_WRITE
);

  wire decoder_1_out0, decoder_1_out6, decoder_1_out7, nor_1_out, not_2_out, or_1_out;

  Decoder #(.select(4)) decoder_1 (
    .out0(decoder_1_out0), .out1(ALU_ADD), .out2(ALU_XOR), .out3(ALU_AND), .out4(R_MUX_MEMORY),
    .out5(R_MUX_MEMORY), .out6(decoder_1_out6), .out7(decoder_1_out7), .out10(R_MUX_IR), .sel(opcode));  // open: out8, out9, out11, out12, out13, out14, out15, en
  and and_1 (Memory_WRITE, decoder_1_out6, Execute_WRITE);
  or or_1 (or_1_out, ALU_ADD, ALU_XOR, ALU_AND, R_MUX_IR);
  nor nor_1 (nor_1_out, R[0], R[1], R[2], R[3], R[4], R[5], R[6], R[7]);
  and and_2 (HALT, decoder_1_out0, Execute);
  or or_2 (R_MUX_ALU, ALU_ADD, Execute, ALU_AND);
  or or_3 (ADDR_MUX_IR, ALU_ADD, ALU_XOR, ALU_AND, R_MUX_MEMORY, R_MUX_MEMORY);
  and and_3 (PC_LOAD, decoder_1_out7, nor_1_out, Execute_WRITE);
  not not_1 (R_WRITE, not_2_out);
  not not_2 (not_2_out, or_1_out);

  assign ADDR_MUX_PC = Fetch;
  assign IR_WRITE = Fetch_Write;
  assign PC_INCREMENT = Fetch;
  assign PC_WRITE = Fetch_Write;
endmodule

module or_gate_3 (
  input  in_1,
  input  in_2,
  input  in_3,
  output out_4
);

  wire pull_resistor_1_node;

  Pull_Resistor #(.pull(1)) pull_resistor_1 (.node(pull_resistor_1_node));
  Transistor #(.\type ("n")) transistor_1 (.in(1'b0), .out(pull_resistor_1_node), .gate(in_1));
  Transistor #(.\type ("n")) transistor_2 (.in(1'b0), .out(pull_resistor_1_node), .gate(in_2));
  Transistor #(.\type ("n")) transistor_3 (.in(1'b0), .out(pull_resistor_1_node), .gate(in_3));
  Transistor #(.\type ("n")) transistor_4 (.in(1'b0), .out(out_4), .gate(pull_resistor_1_node));
  Pull_Resistor #(.pull(1)) pull_resistor_2 (.node(out_4));
endmodule

module register_8bit_v2 (
  input  Write,
  input  [7:0] Data_In,
  output [7:0] Data_Out
);

  D_Flip_Flop d_ff_1 (.D(Data_In[0]), .clk(Write), .Q(Data_Out[0]));  // open: Qn, preset, reset
  D_Flip_Flop d_ff_2 (.D(Data_In[1]), .clk(Write), .Q(Data_Out[1]));  // open: Qn, preset, reset
  D_Flip_Flop d_ff_3 (.D(Data_In[2]), .clk(Write), .Q(Data_Out[2]));  // open: Qn, preset, reset
  D_Flip_Flop d_ff_4 (.D(Data_In[3]), .clk(Write), .Q(Data_Out[3]));  // open: Qn, preset, reset
  D_Flip_Flop d_ff_5 (.D(Data_In[4]), .clk(Write), .Q(Data_Out[4]));  // open: Qn, preset, reset
  D_Flip_Flop d_ff_6 (.D(Data_In[5]), .clk(Write), .Q(Data_Out[5]));  // open: Qn, preset, reset
  D_Flip_Flop d_ff_7 (.D(Data_In[6]), .clk(Write), .Q(Data_Out[6]));  // open: Qn, preset, reset
  D_Flip_Flop d_ff_8 (.D(Data_In[7]), .clk(Write), .Q(Data_Out[7]));  // open: Qn, preset, reset
endmodule

module odd (
  input  A,
  input  B,
  input  C,
  output O
);

  ExactlyOne xor_1 (.out(O), .in0(A), .in1(B), .in2(C));
endmodule

module maj (
  input  A,
  input  B,
  input  C,
  output O
);

  wire and_1_out, and_2_out, and_3_out;

  and and_1 (and_1_out, A, B);
  and and_2 (and_2_out, A, C);
  and and_3 (and_3_out, C, B);
  or or_1 (O, and_1_out, and_2_out, and_3_out);
endmodule

module Full_adder_majANDodd (
  input  A,
  input  B,
  input  Carry,
  output Sum,
  output Cout
);

  odd odd_1 (.A(A), .B(B), .C(Carry), .O(Sum));
  maj maj_1 (.A(A), .B(B), .C(Carry), .O(Cout));
endmodule

module Sub (
  input  [7:0] A,
  input  [7:0] B,
  input  SUB,
  output [7:0] out_4
);

  wire [7:0] xor_1_out;

  assign xor_1_out = {8{SUB}} ^ B;  // XOR_Gate xor_1, 8 bits wide
  fulladder_8bit_majODD fulladder_8bit_majodd_1 (.CIN(SUB), .A(A), .B(xor_1_out), .OUT1(out_4));
endmodule

module fulladder_8bit_majODD (
  input  CIN,
  input  [7:0] A,
  input  [7:0] B,
  output [7:0] OUT1
);

  wire full_adder_majandodd_1_cout, full_adder_majandodd_2_cout, full_adder_majandodd_3_cout,
       full_adder_majandodd_4_cout, full_adder_majandodd_5_cout, full_adder_majandodd_6_cout,
       full_adder_majandodd_7_cout;

  Full_adder_majANDodd full_adder_majandodd_1 (
    .A(A[0]), .B(B[0]), .Carry(CIN), .Sum(OUT1[0]), .Cout(full_adder_majandodd_1_cout));
  Full_adder_majANDodd full_adder_majandodd_2 (
    .A(A[1]), .B(B[1]), .Carry(full_adder_majandodd_1_cout), .Sum(OUT1[1]), .Cout(full_adder_majandodd_2_cout));
  Full_adder_majANDodd full_adder_majandodd_3 (
    .A(A[2]), .B(B[2]), .Carry(full_adder_majandodd_2_cout), .Sum(OUT1[2]), .Cout(full_adder_majandodd_3_cout));
  Full_adder_majANDodd full_adder_majandodd_4 (
    .A(A[3]), .B(B[3]), .Carry(full_adder_majandodd_3_cout), .Sum(OUT1[3]), .Cout(full_adder_majandodd_4_cout));
  Full_adder_majANDodd full_adder_majandodd_5 (
    .A(A[4]), .B(B[4]), .Carry(full_adder_majandodd_4_cout), .Sum(OUT1[4]), .Cout(full_adder_majandodd_5_cout));
  Full_adder_majANDodd full_adder_majandodd_6 (
    .A(A[5]), .B(B[5]), .Carry(full_adder_majandodd_5_cout), .Sum(OUT1[5]), .Cout(full_adder_majandodd_6_cout));
  Full_adder_majANDodd full_adder_majandodd_7 (
    .A(A[6]), .B(B[6]), .Carry(full_adder_majandodd_6_cout), .Sum(OUT1[6]), .Cout(full_adder_majandodd_7_cout));
  Full_adder_majANDodd full_adder_majandodd_8 (
    .A(A[7]), .B(B[7]), .Carry(full_adder_majandodd_7_cout), .Sum(OUT1[7]));  // open: Cout
endmodule

module demux_3to8 (
  input  InputBus,
  input  [2:0] Sel,
  output O0,
  output O1,
  output O2,
  output O3,
  output O4,
  output O5,
  output O6,
  output O7
);

  wire not_1_out, not_2_out, not_3_out;

  not not_1 (not_1_out, Sel[0]);
  not not_2 (not_2_out, Sel[1]);
  not not_3 (not_3_out, Sel[2]);
  and and_1 (O0, InputBus, not_1_out, not_2_out, not_3_out);
  and and_2 (O1, InputBus, Sel[0], not_2_out, not_3_out);
  and and_3 (O2, InputBus, Sel[1], not_1_out, not_3_out);
  and and_4 (O3, InputBus, Sel[1], Sel[0], not_3_out);
  and and_5 (O4, InputBus, Sel[2], not_1_out, not_2_out);
  and and_6 (O5, InputBus, Sel[2], not_2_out, Sel[0]);
  and and_7 (O6, InputBus, Sel[2], Sel[1], not_1_out);
  and and_8 (O7, InputBus, Sel[2], Sel[1], Sel[0]);
endmodule

module Main_CPU (
);

  wire and_1_out, and_2_out, clock_1_out, control_unit_1_addr_mux_ir, control_unit_1_alu_add,
       control_unit_1_alu_and, control_unit_1_alu_xor, control_unit_1_ir_write, control_unit_1_memory_write,
       control_unit_1_pc_load, control_unit_1_pc_write, control_unit_1_r_write, d_ff_1_q, d_ff_1_qn,
       not_1_out;
  wire [1:0] control_unit_1_r_mux_ir;
  wire [3:0] multiplexer_1_out, program_counter_1_outputbus;
  wire [7:0] alu_final_1_out1, multiplexer_2_out, ram_1_dout, register_8bit_1_data_out,
       register_8bit_2_data_out;

  Control_Unit control_unit_1 (
    .opcode(register_8bit_1_data_out[7:4]), .Fetch(d_ff_1_q), .Fetch_Write(and_1_out), .Execute(d_ff_1_qn),
    .Execute_WRITE(and_2_out), .R(register_8bit_2_data_out), .ALU_ADD(control_unit_1_alu_add),
    .ALU_XOR(control_unit_1_alu_xor), .ALU_AND(control_unit_1_alu_and),
    .Memory_WRITE(control_unit_1_memory_write), .R_MUX_MEMORY(control_unit_1_r_mux_ir[1]),
    .R_MUX_IR(control_unit_1_r_mux_ir[0]), .R_WRITE(control_unit_1_r_write),
    .PC_LOAD(control_unit_1_pc_load), .PC_WRITE(control_unit_1_pc_write),
    .ADDR_MUX_IR(control_unit_1_addr_mux_ir), .IR_WRITE(control_unit_1_ir_write));  // open: HALT, R_MUX_ALU, PC_INCREMENT, ADDR_MUX_PC
  Program_Counter program_counter_1 (
    .InputBus(register_8bit_1_data_out[3:0]), .LOAD(control_unit_1_pc_load), .WRITE(control_unit_1_pc_write),
    .OutputBus(program_counter_1_outputbus));
  ALU_final alu_final_1 (
    .A(register_8bit_2_data_out), .B(ram_1_dout), .ADD(control_unit_1_alu_add),
    .AND1(control_unit_1_alu_and), .XOR1(control_unit_1_alu_xor), .OUT1(alu_final_1_out1));  // open: SUB, LSHIFT, RSHIFT
  Clock clock_1 (.out(clock_1_out));
  Multiplexer #(.width(4)) multiplexer_1 (
    .in0(program_counter_1_outputbus), .in1(register_8bit_1_data_out[3:0]), .out(multiplexer_1_out),
    .sel(control_unit_1_addr_mux_ir));
  D_Flip_Flop d_ff_1 (.D(d_ff_1_qn), .clk(clock_1_out), .Q(d_ff_1_q), .Qn(d_ff_1_qn));  // open: preset, reset
  RAM #(.addrWidth(4)) ram_1 (
    .addr(multiplexer_1_out), .we(control_unit_1_memory_write), .oe(not_1_out),
    .din(register_8bit_2_data_out), .dout(ram_1_dout));  // open: clk
  not not_1 (not_1_out, control_unit_1_memory_write);
  and and_1 (and_1_out, d_ff_1_q, clock_1_out);
  and and_2 (and_2_out, d_ff_1_qn, clock_1_out);
  Multiplexer #(.select(2), .width(8)) multiplexer_2 (
    .in0(alu_final_1_out1), .in1(ram_1_dout),
    .in2({register_8bit_1_data_out[3:0], register_8bit_1_data_out[3:0]}), .in3({8{1'b0}}),
    .out(multiplexer_2_out), .sel(control_unit_1_r_mux_ir));
  Register_8bit register_8bit_1 (
    .Write(control_unit_1_ir_write), .Data_In(ram_1_dout), .Data_Out(register_8bit_1_data_out));
  Register_8bit register_8bit_2 (
    .Write(control_unit_1_r_write), .Data_In(multiplexer_2_out), .Data_Out(register_8bit_2_data_out));
endmodule

module Memory_Bit (
  input  INPUT1,
  input  Write,
  output OUTPUT1
);

  D_Flip_Flop d_ff_1 (.D(INPUT1), .clk(Write), .Q(OUTPUT1));  // open: Qn, preset, reset
endmodule

module CPU_v2 (
);

  wire and_1_out, clock_1_out, control_unit_1_alu_add, control_unit_1_alu_and, control_unit_1_alu_xor,
       control_unit_1_halt, control_unit_1_ir_write, control_unit_1_memory_write, control_unit_1_pc_load,
       control_unit_1_pc_write, control_unit_1_r_mux_ir, control_unit_1_r_write, decoder_1_out0,
       decoder_1_out1, decoder_1_out2, decoder_1_out3, not_1_out, not_2_out;
  wire [1:0] control_unit_1_r_mux_memory, phase_counter_1_out_2;
  wire [3:0] program_counter_1_outputbus;
  wire [7:0] alu_final_1_out1, multiplexer_1_out, ram_1_dout, register_1_q, register_2_q;

  // Probe on ram_1_dout
  // Probe on ram_1_dout
  // Probe on register_1_q
  Control_Unit control_unit_1 (
    .opcode(register_2_q[7:4]), .Fetch(decoder_1_out0), .Fetch_Write(decoder_1_out1),
    .Execute(decoder_1_out2), .Execute_WRITE(decoder_1_out3), .HALT(control_unit_1_halt),
    .ALU_ADD(control_unit_1_alu_add), .ALU_XOR(control_unit_1_alu_xor), .ALU_AND(control_unit_1_alu_and),
    .Memory_WRITE(control_unit_1_memory_write), .R_MUX_ALU(control_unit_1_r_mux_memory[1]),
    .R_MUX_MEMORY(control_unit_1_r_mux_memory[0]), .R_MUX_IR(control_unit_1_r_mux_ir),
    .R_WRITE(control_unit_1_r_write), .PC_LOAD(control_unit_1_pc_load), .PC_WRITE(control_unit_1_pc_write),
    .IR_WRITE(control_unit_1_ir_write));  // open: R, PC_INCREMENT, ADDR_MUX_PC, ADDR_MUX_IR
  Program_Counter program_counter_1 (
    .InputBus(register_2_q[3:0]), .LOAD(control_unit_1_pc_load), .WRITE(control_unit_1_pc_write),
    .OutputBus(program_counter_1_outputbus));
  ALU_final alu_final_1 (
    .A(register_1_q), .B(ram_1_dout), .ADD(control_unit_1_alu_add), .AND1(control_unit_1_alu_and),
    .XOR1(control_unit_1_alu_xor), .OUT1(alu_final_1_out1));  // open: SUB, LSHIFT, RSHIFT
  // Probe on control_unit_1_alu_add
  // Probe on alu_final_1_out1
  // Probe on control_unit_1_r_mux_memory
  Phase_Counter phase_counter_1 (.Clock(and_1_out), .out_2(phase_counter_1_out_2));
  not not_1 (not_1_out, control_unit_1_halt);
  Clock clock_1 (.out(clock_1_out));
  Decoder #(.select(2)) decoder_1 (
    .out0(decoder_1_out0), .out1(decoder_1_out1), .out2(decoder_1_out2), .out3(decoder_1_out3),
    .sel(phase_counter_1_out_2));  // open: en
  and and_1 (and_1_out, not_1_out, clock_1_out);
  not not_2 (not_2_out, control_unit_1_memory_write);
  RAM #(.addrWidth(4)) ram_1 (
    .addr(program_counter_1_outputbus), .we(control_unit_1_memory_write), .oe(not_2_out), .clk(and_1_out),
    .din(register_1_q), .dout(ram_1_dout));
  Multiplexer #(.select(2), .width(8)) multiplexer_1 (
    .in0(alu_final_1_out1), .in1(ram_1_dout), .in2({4'b0000, register_2_q[3:0]}), .in3({8{1'b0}}),
    .out(multiplexer_1_out), .sel(control_unit_1_r_mux_memory));
  Register #(.trigger("falling")) register_1 (
    .D(multiplexer_1_out), .en(control_unit_1_r_write), .clk(and_1_out), .Q(register_1_q));  // open: clr
  Register #(.trigger("falling")) register_2 (
    .D(ram_1_dout), .en(control_unit_1_ir_write), .clk(and_1_out), .Q(register_2_q));  // open: clr
  // Probe on multiplexer_1_out
  // Probe on control_unit_1_r_mux_memory
endmodule

module Phase_Counter (
  input  Clock,
  output [1:0] out_2
);

  wire d_ff_2_qn, xor_1_out;

  xor xor_1 (xor_1_out, out_2[1], out_2[0]);
  D_Flip_Flop d_ff_1 (.D(xor_1_out), .clk(Clock), .Q(out_2[1]));  // open: Qn, preset, reset
  D_Flip_Flop d_ff_2 (.D(d_ff_2_qn), .clk(Clock), .Q(out_2[0]), .Qn(d_ff_2_qn));  // open: preset, reset
endmodule

module ALU_16_bit (
  input  [15:0] A,
  input  [15:0] B,
  input  ADD,
  input  AND1,
  input  XOR1,
  input  SUB,
  input  LSHIFT,
  input  RSHIFT,
  output Zero,
  output [15:0] OUT1,
  output Positive
);

  wire [15:0] and_1_out, and_2_out, and_3_out, and_4_out, and_5_out, and_6_out, and_gate_16_bit_1_out1,
       full_adder_16bit_1_out1, lshift_16bit_1_out_4, rshift_16bit_1_out_3, sub_16bit_1_out_4,
       xor_gate_16bit_1_out1;

  SUB_16bit sub_16bit_1 (.A(A), .B(B), .SUB(SUB), .out_4(sub_16bit_1_out_4));
  lshift_16bit lshift_16bit_1 (.in_1(A), .CIN(1'b0), .EN(LSHIFT), .out_4(lshift_16bit_1_out_4));
  rshift_16bit rshift_16bit_1 (.in_1(A), .EN(RSHIFT), .out_3(rshift_16bit_1_out_3));
  full_adder_16bit full_adder_16bit_1 (.A(A), .B(B), .OUT1(full_adder_16bit_1_out1));  // open: CIN
  and_gate_16_bit and_gate_16_bit_1 (.A(A), .B(B), .OUT1(and_gate_16_bit_1_out1));
  XOR_gate_16bit xor_gate_16bit_1 (.A(A), .B(B), .OUT1(xor_gate_16bit_1_out1));
  assign and_1_out = full_adder_16bit_1_out1 & {16{ADD}};  // AND_Gate and_1, 16 bits wide
  assign and_2_out = and_gate_16_bit_1_out1 & {16{AND1}};  // AND_Gate and_2, 16 bits wide
  assign and_3_out = xor_gate_16bit_1_out1 & {16{XOR1}};  // AND_Gate and_3, 16 bits wide
  assign and_4_out = sub_16bit_1_out_4 & {16{SUB}};  // AND_Gate and_4, 16 bits wide
  assign and_5_out = lshift_16bit_1_out_4 & {16{LSHIFT}};  // AND_Gate and_5, 16 bits wide
  assign and_6_out = rshift_16bit_1_out_3 & {16{RSHIFT}};  // AND_Gate and_6, 16 bits wide
  assign OUT1 = and_5_out | and_1_out | and_4_out | and_2_out | and_3_out | and_6_out;  // OR_Gate or_1, 16 bits wide
  Comparator #(.width(16)) comparator_1 (.a(OUT1), .b({16{1'b0}}), .gt(Positive), .eq(Zero));  // open: lt
endmodule

module full_adder_16bit (
  input  CIN,
  input  [15:0] A,
  input  [15:0] B,
  output [15:0] OUT1
);

  wire full_adder_majandodd_1_cout, full_adder_majandodd_2_cout, full_adder_majandodd_3_cout,
       full_adder_majandodd_4_cout, full_adder_majandodd_5_cout, full_adder_majandodd_6_cout,
       full_adder_majandodd_7_cout, full_adder_majandodd_8_cout, full_adder_majandodd_9_cout,
       full_adder_majandodd_10_cout, full_adder_majandodd_11_cout, full_adder_majandodd_12_cout,
       full_adder_majandodd_13_cout, full_adder_majandodd_14_cout, full_adder_majandodd_15_cout;

  Full_adder_majANDodd full_adder_majandodd_1 (
    .A(A[0]), .B(B[0]), .Carry(CIN), .Sum(OUT1[0]), .Cout(full_adder_majandodd_1_cout));
  Full_adder_majANDodd full_adder_majandodd_2 (
    .A(A[1]), .B(B[1]), .Carry(full_adder_majandodd_1_cout), .Sum(OUT1[1]), .Cout(full_adder_majandodd_2_cout));
  Full_adder_majANDodd full_adder_majandodd_3 (
    .A(A[2]), .B(B[2]), .Carry(full_adder_majandodd_2_cout), .Sum(OUT1[2]), .Cout(full_adder_majandodd_3_cout));
  Full_adder_majANDodd full_adder_majandodd_4 (
    .A(A[3]), .B(B[3]), .Carry(full_adder_majandodd_3_cout), .Sum(OUT1[3]), .Cout(full_adder_majandodd_4_cout));
  Full_adder_majANDodd full_adder_majandodd_5 (
    .A(A[4]), .B(B[4]), .Carry(full_adder_majandodd_4_cout), .Sum(OUT1[4]), .Cout(full_adder_majandodd_5_cout));
  Full_adder_majANDodd full_adder_majandodd_6 (
    .A(A[5]), .B(B[5]), .Carry(full_adder_majandodd_5_cout), .Sum(OUT1[5]), .Cout(full_adder_majandodd_6_cout));
  Full_adder_majANDodd full_adder_majandodd_7 (
    .A(A[6]), .B(B[6]), .Carry(full_adder_majandodd_6_cout), .Sum(OUT1[6]), .Cout(full_adder_majandodd_7_cout));
  Full_adder_majANDodd full_adder_majandodd_8 (
    .A(A[7]), .B(B[7]), .Carry(full_adder_majandodd_7_cout), .Sum(OUT1[7]), .Cout(full_adder_majandodd_8_cout));
  Full_adder_majANDodd full_adder_majandodd_9 (
    .A(A[8]), .B(B[8]), .Carry(full_adder_majandodd_8_cout), .Sum(OUT1[8]), .Cout(full_adder_majandodd_9_cout));
  Full_adder_majANDodd full_adder_majandodd_10 (
    .A(A[9]), .B(B[9]), .Carry(full_adder_majandodd_9_cout), .Sum(OUT1[9]),
    .Cout(full_adder_majandodd_10_cout));
  Full_adder_majANDodd full_adder_majandodd_11 (
    .A(A[10]), .B(B[10]), .Carry(full_adder_majandodd_10_cout), .Sum(OUT1[10]),
    .Cout(full_adder_majandodd_11_cout));
  Full_adder_majANDodd full_adder_majandodd_12 (
    .A(A[11]), .B(B[11]), .Carry(full_adder_majandodd_11_cout), .Sum(OUT1[11]),
    .Cout(full_adder_majandodd_12_cout));
  Full_adder_majANDodd full_adder_majandodd_13 (
    .A(A[12]), .B(B[12]), .Carry(full_adder_majandodd_12_cout), .Sum(OUT1[12]),
    .Cout(full_adder_majandodd_13_cout));
  Full_adder_majANDodd full_adder_majandodd_14 (
    .A(A[13]), .B(B[13]), .Carry(full_adder_majandodd_13_cout), .Sum(OUT1[13]),
    .Cout(full_adder_majandodd_14_cout));
  Full_adder_majANDodd full_adder_majandodd_15 (
    .A(A[14]), .B(B[14]), .Carry(full_adder_majandodd_14_cout), .Sum(OUT1[14]),
    .Cout(full_adder_majandodd_15_cout));
  Full_adder_majANDodd full_adder_majandodd_16 (
    .A(A[15]), .B(B[15]), .Carry(full_adder_majandodd_15_cout), .Sum(OUT1[15]));  // open: Cout
endmodule

module and_gate_16_bit (
  input  [15:0] A,
  input  [15:0] B,
  output [15:0] OUT1
);

  and_gate_design_2 and_gate_design_2_1 (.in_1(A[0]), .in_2(B[0]), .out_3(OUT1[0]));
  and_gate_design_2 and_gate_design_2_2 (.in_1(A[1]), .in_2(B[1]), .out_3(OUT1[1]));
  and_gate_design_2 and_gate_design_2_3 (.in_1(A[2]), .in_2(B[2]), .out_3(OUT1[2]));
  and_gate_design_2 and_gate_design_2_4 (.in_1(A[3]), .in_2(B[3]), .out_3(OUT1[3]));
  and_gate_design_2 and_gate_design_2_5 (.in_1(A[4]), .in_2(B[4]), .out_3(OUT1[4]));
  and_gate_design_2 and_gate_design_2_6 (.in_1(A[5]), .in_2(B[5]), .out_3(OUT1[5]));
  and_gate_design_2 and_gate_design_2_7 (.in_1(A[6]), .in_2(B[6]), .out_3(OUT1[6]));
  and_gate_design_2 and_gate_design_2_8 (.in_1(A[7]), .in_2(B[7]), .out_3(OUT1[7]));
  and_gate_design_2 and_gate_design_2_9 (.in_1(A[8]), .in_2(B[8]), .out_3(OUT1[8]));
  and_gate_design_2 and_gate_design_2_10 (.in_1(A[9]), .in_2(B[9]), .out_3(OUT1[9]));
  and_gate_design_2 and_gate_design_2_11 (.in_1(A[10]), .in_2(B[10]), .out_3(OUT1[10]));
  and_gate_design_2 and_gate_design_2_12 (.in_1(A[11]), .in_2(B[11]), .out_3(OUT1[11]));
  and_gate_design_2 and_gate_design_2_13 (.in_1(A[12]), .in_2(B[12]), .out_3(OUT1[12]));
  and_gate_design_2 and_gate_design_2_14 (.in_1(A[13]), .in_2(B[13]), .out_3(OUT1[13]));
  and_gate_design_2 and_gate_design_2_15 (.in_1(A[14]), .in_2(B[14]), .out_3(OUT1[14]));
  and_gate_design_2 and_gate_design_2_16 (.in_1(A[15]), .in_2(B[15]), .out_3(OUT1[15]));
endmodule

module XOR_gate_16bit (
  input  [15:0] A,
  input  [15:0] B,
  output [15:0] OUT1
);

  XOR_GATE xor_gate_1 (.in_1(A[0]), .in_2(B[0]), .out_3(OUT1[0]));
  XOR_GATE xor_gate_2 (.in_1(A[1]), .in_2(B[1]), .out_3(OUT1[1]));
  XOR_GATE xor_gate_3 (.in_1(A[2]), .in_2(B[2]), .out_3(OUT1[2]));
  XOR_GATE xor_gate_4 (.in_1(A[3]), .in_2(B[3]), .out_3(OUT1[3]));
  XOR_GATE xor_gate_5 (.in_1(A[4]), .in_2(B[4]), .out_3(OUT1[4]));
  XOR_GATE xor_gate_6 (.in_1(A[5]), .in_2(B[5]), .out_3(OUT1[5]));
  XOR_GATE xor_gate_7 (.in_1(A[6]), .in_2(B[6]), .out_3(OUT1[6]));
  XOR_GATE xor_gate_8 (.in_1(A[7]), .in_2(B[7]), .out_3(OUT1[7]));
  XOR_GATE xor_gate_9 (.in_1(A[8]), .in_2(B[8]), .out_3(OUT1[8]));
  XOR_GATE xor_gate_10 (.in_1(A[9]), .in_2(B[9]), .out_3(OUT1[9]));
  XOR_GATE xor_gate_11 (.in_1(A[10]), .in_2(B[10]), .out_3(OUT1[10]));
  XOR_GATE xor_gate_12 (.in_1(A[11]), .in_2(B[11]), .out_3(OUT1[11]));
  XOR_GATE xor_gate_13 (.in_1(A[12]), .in_2(B[12]), .out_3(OUT1[12]));
  XOR_GATE xor_gate_14 (.in_1(A[13]), .in_2(B[13]), .out_3(OUT1[13]));
  XOR_GATE xor_gate_15 (.in_1(A[14]), .in_2(B[14]), .out_3(OUT1[14]));
  XOR_GATE xor_gate_16 (.in_1(A[15]), .in_2(B[15]), .out_3(OUT1[15]));
endmodule

module lshift_16bit (
  input  [15:0] in_1,
  input  CIN,
  input  EN,
  output [15:0] out_4
);

  Multiplexer multiplexer_1 (.in0(in_1[15]), .in1(in_1[14]), .out(out_4[15]), .sel(EN));
  Multiplexer multiplexer_2 (.in0(in_1[14]), .in1(in_1[13]), .out(out_4[14]), .sel(EN));
  Multiplexer multiplexer_3 (.in0(in_1[13]), .in1(in_1[12]), .out(out_4[13]), .sel(EN));
  Multiplexer multiplexer_4 (.in0(in_1[12]), .in1(in_1[11]), .out(out_4[12]), .sel(EN));
  Multiplexer multiplexer_5 (.in0(in_1[11]), .in1(in_1[10]), .out(out_4[11]), .sel(EN));
  Multiplexer multiplexer_6 (.in0(in_1[10]), .in1(in_1[9]), .out(out_4[10]), .sel(EN));
  Multiplexer multiplexer_7 (.in0(in_1[9]), .in1(in_1[8]), .out(out_4[9]), .sel(EN));
  Multiplexer multiplexer_8 (.in0(in_1[8]), .in1(in_1[7]), .out(out_4[8]), .sel(EN));
  Multiplexer multiplexer_9 (.in0(in_1[7]), .in1(in_1[6]), .out(out_4[7]), .sel(EN));
  Multiplexer multiplexer_10 (.in0(in_1[6]), .in1(in_1[5]), .out(out_4[6]), .sel(EN));
  Multiplexer multiplexer_11 (.in0(in_1[5]), .in1(in_1[4]), .out(out_4[5]), .sel(EN));
  Multiplexer multiplexer_12 (.in0(in_1[4]), .in1(in_1[3]), .out(out_4[4]), .sel(EN));
  Multiplexer multiplexer_13 (.in0(in_1[3]), .in1(in_1[2]), .out(out_4[3]), .sel(EN));
  Multiplexer multiplexer_14 (.in0(in_1[2]), .in1(in_1[1]), .out(out_4[2]), .sel(EN));
  Multiplexer multiplexer_15 (.in0(in_1[1]), .in1(in_1[0]), .out(out_4[1]), .sel(EN));
  Multiplexer multiplexer_16 (.in0(in_1[0]), .in1(CIN), .out(out_4[0]), .sel(EN));
endmodule

module rshift_16bit (
  input  [15:0] in_1,
  input  EN,
  output [15:0] out_3
);

  Multiplexer multiplexer_1 (.in0(in_1[15]), .in1(1'b0), .out(out_3[15]), .sel(EN));
  Multiplexer multiplexer_2 (.in0(in_1[14]), .in1(in_1[15]), .out(out_3[14]), .sel(EN));
  Multiplexer multiplexer_3 (.in0(in_1[13]), .in1(in_1[14]), .out(out_3[13]), .sel(EN));
  Multiplexer multiplexer_4 (.in0(in_1[12]), .in1(in_1[13]), .out(out_3[12]), .sel(EN));
  Multiplexer multiplexer_5 (.in0(in_1[11]), .in1(in_1[12]), .out(out_3[11]), .sel(EN));
  Multiplexer multiplexer_6 (.in0(in_1[10]), .in1(in_1[11]), .out(out_3[10]), .sel(EN));
  Multiplexer multiplexer_7 (.in0(in_1[9]), .in1(in_1[10]), .out(out_3[9]), .sel(EN));
  Multiplexer multiplexer_8 (.in0(in_1[8]), .in1(in_1[9]), .out(out_3[8]), .sel(EN));
  Multiplexer multiplexer_9 (.in0(in_1[7]), .in1(in_1[8]), .out(out_3[7]), .sel(EN));
  Multiplexer multiplexer_10 (.in0(in_1[6]), .in1(in_1[7]), .out(out_3[6]), .sel(EN));
  Multiplexer multiplexer_11 (.in0(in_1[5]), .in1(in_1[6]), .out(out_3[5]), .sel(EN));
  Multiplexer multiplexer_12 (.in0(in_1[4]), .in1(in_1[5]), .out(out_3[4]), .sel(EN));
  Multiplexer multiplexer_13 (.in0(in_1[3]), .in1(in_1[4]), .out(out_3[3]), .sel(EN));
  Multiplexer multiplexer_14 (.in0(in_1[2]), .in1(in_1[3]), .out(out_3[2]), .sel(EN));
  Multiplexer multiplexer_15 (.in0(in_1[1]), .in1(in_1[2]), .out(out_3[1]), .sel(EN));
  Multiplexer multiplexer_16 (.in0(in_1[0]), .in1(in_1[1]), .out(out_3[0]), .sel(EN));
endmodule

module SUB_16bit (
  input  [15:0] A,
  input  [15:0] B,
  input  SUB,
  output [15:0] out_4
);

  wire [15:0] xor_1_out;

  assign xor_1_out = {16{SUB}} ^ B;  // XOR_Gate xor_1, 16 bits wide
  full_adder_16bit full_adder_16bit_1 (.CIN(SUB), .A(A), .B(xor_1_out), .OUT1(out_4));
endmodule

module ProgramCounter_16bit (
  input  [7:0] InputBus,
  input  LOAD,
  input  WRITE,
  output [7:0] OutputBus
);

  wire [7:0] incrementer_8bit_1_x_inc, multiplexer_1_out;

  Register register_1 (.D(multiplexer_1_out), .clk(WRITE), .Q(OutputBus));  // open: en, clr
  Multiplexer #(.width(8)) multiplexer_1 (
    .in0(incrementer_8bit_1_x_inc), .in1(InputBus), .out(multiplexer_1_out), .sel(LOAD));
  incrementer_8bit incrementer_8bit_1 (.X(OutputBus), .x_inc(incrementer_8bit_1_x_inc));
endmodule

module incrementer_8bit (
  input  [7:0] X,
  output [7:0] x_inc
);

  wire and_1_out, and_2_out, and_3_out, and_4_out, and_5_out, and_6_out, and_7_out;

  and and_1 (and_1_out, X[0], 1'b1);
  and and_2 (and_2_out, X[1], and_1_out);
  and and_3 (and_3_out, X[2], and_2_out);
  and and_4 (and_4_out, X[3], and_3_out);
  buf and_5 (and_5_out, X[4]);  // AND_Gate
  and and_6 (and_6_out, X[5], and_5_out);
  and and_7 (and_7_out, X[6], and_6_out);
  // AND_Gate and_8 has open pins: in0=X[7], in1=and_7_out, out=open
  xor xor_1 (x_inc[0], X[0], 1'b1);
  xor xor_2 (x_inc[1], X[1], and_1_out);
  xor xor_3 (x_inc[2], X[2], and_2_out);
  xor xor_4 (x_inc[3], X[3], and_3_out);
  xor xor_5 (x_inc[4], and_4_out, X[4]);
  xor xor_6 (x_inc[5], X[5], and_5_out);
  xor xor_7 (x_inc[6], X[6], and_6_out);
  xor xor_8 (x_inc[7], X[7], and_7_out);
endmodule

module Register_16bit (
  input  Write,
  input  [15:0] Data_In,
  output [15:0] Data_Out
);

  D_Flip_Flop d_ff_1 (.D(Data_In[0]), .clk(Write), .Q(Data_Out[0]));  // open: Qn, preset, reset
  D_Flip_Flop d_ff_2 (.D(Data_In[1]), .clk(Write), .Q(Data_Out[1]));  // open: Qn, preset, reset
  D_Flip_Flop d_ff_3 (.D(Data_In[2]), .clk(Write), .Q(Data_Out[2]));  // open: Qn, preset, reset
  D_Flip_Flop d_ff_4 (.D(Data_In[3]), .clk(Write), .Q(Data_Out[3]));  // open: Qn, preset, reset
  D_Flip_Flop d_ff_5 (.D(Data_In[4]), .clk(Write), .Q(Data_Out[4]));  // open: Qn, preset, reset
  D_Flip_Flop d_ff_6 (.D(Data_In[5]), .clk(Write), .Q(Data_Out[5]));  // open: Qn, preset, reset
  D_Flip_Flop d_ff_7 (.D(Data_In[6]), .clk(Write), .Q(Data_Out[6]));  // open: Qn, preset, reset
  D_Flip_Flop d_ff_8 (.D(Data_In[7]), .clk(Write), .Q(Data_Out[7]));  // open: Qn, preset, reset
  D_Flip_Flop d_ff_9 (.D(Data_In[8]), .clk(Write), .Q(Data_Out[8]));  // open: Qn, preset, reset
  D_Flip_Flop d_ff_10 (.D(Data_In[9]), .clk(Write), .Q(Data_Out[9]));  // open: Qn, preset, reset
  D_Flip_Flop d_ff_11 (.D(Data_In[10]), .clk(Write), .Q(Data_Out[10]));  // open: Qn, preset, reset
  D_Flip_Flop d_ff_12 (.D(Data_In[11]), .clk(Write), .Q(Data_Out[11]));  // open: Qn, preset, reset
  D_Flip_Flop d_ff_13 (.D(Data_In[12]), .clk(Write), .Q(Data_Out[12]));  // open: Qn, preset, reset
  D_Flip_Flop d_ff_14 (.D(Data_In[14]), .clk(Write), .Q(Data_Out[14]));  // open: Qn, preset, reset
  D_Flip_Flop d_ff_15 (.D(Data_In[13]), .clk(Write), .Q(Data_Out[13]));  // open: Qn, preset, reset
  D_Flip_Flop d_ff_16 (.D(Data_In[15]), .clk(Write), .Q(Data_Out[15]));  // open: Qn, preset, reset
endmodule

module Register_file (
  input  [3:0] rs_addr,
  input  [3:0] rt_addr,
  input  [3:0] rd_addr,
  input  [15:0] Write_Data,
  input  Reg_Write,
  input  Read_Rd_Mux,
  input  Clock,
  output [15:0] rs_data,
  output [15:0] rt_data
);

  wire and_1_out, comparator_1_eq, not_1_out, not_2_out;
  wire [3:0] multiplexer_1_out, multiplexer_2_out;
  wire [15:0] controlled_buffer_1_out;

  assign controlled_buffer_1_out = and_1_out ? Write_Data : 16'bz;  // Controlled_Buffer controlled_buffer_1
  RAM #(.addrWidth(4), .dataWidth(16), .\type ("nonvolatile")) ram_1 (
    .addr(multiplexer_1_out), .we(and_1_out), .oe(1'b1), .clk(Clock), .din(controlled_buffer_1_out),
    .dout(rs_data));
  RAM #(.addrWidth(4), .dataWidth(16), .\type ("nonvolatile")) ram_2 (
    .addr(multiplexer_2_out), .we(and_1_out), .oe(1'b1), .clk(Clock), .din(controlled_buffer_1_out),
    .dout(rt_data));
  Comparator #(.width(4)) comparator_1 (.a(rd_addr), .b(4'b0000), .eq(comparator_1_eq));  // open: gt, lt
  not not_1 (not_1_out, comparator_1_eq);
  and and_1 (and_1_out, not_1_out, Reg_Write);
  Multiplexer #(.width(4)) multiplexer_1 (.in0(rs_addr), .in1(rd_addr), .out(multiplexer_1_out), .sel(and_1_out));
  Multiplexer #(.width(4)) multiplexer_2 (.in0(rt_addr), .in1(rd_addr), .out(multiplexer_2_out), .sel(and_1_out));
  not not_2 (not_2_out, and_1_out);
endmodule

module Comparator_4Bit (
  input  A0,
  input  B0,
  input  A1,
  input  B1,
  input  A2,
  input  B2,
  input  A3,
  input  B3,
  output out_9,
  output out_10,
  output out_11
);

  wire and_1_out, and_2_out, and_3_out, and_4_out, and_5_out, and_6_out, and_7_out, and_8_out, and_9_out,
       and_10_out, and_11_out, and_12_out, and_13_out, and_14_out, not_1_out, not_2_out, not_3_out,
       not_4_out, not_5_out, not_6_out, not_7_out, not_8_out, or_1_out, or_2_out, or_3_out, or_4_out;

  not not_1 (not_1_out, A0);
  not not_2 (not_2_out, B0);
  not not_3 (not_3_out, A1);
  not not_4 (not_4_out, B1);
  not not_5 (not_5_out, A2);
  not not_6 (not_6_out, B2);
  not not_7 (not_7_out, A3);
  not not_8 (not_8_out, B3);
  and and_1 (and_1_out, not_7_out, B3);
  and and_2 (and_2_out, A3, not_8_out);
  and and_3 (and_3_out, not_1_out, B0);
  and and_4 (and_4_out, A0, not_2_out);
  and and_5 (and_5_out, not_3_out, B1);
  and and_6 (and_6_out, A1, not_4_out);
  and and_7 (and_7_out, not_5_out, B2);
  and and_8 (and_8_out, A2, not_6_out);
  or or_1 (or_1_out, and_3_out, and_4_out);
  or or_2 (or_2_out, and_5_out, and_6_out);
  or or_3 (or_3_out, and_7_out, and_8_out);
  or or_4 (or_4_out, and_1_out, and_2_out);
  and and_9 (and_9_out, or_1_out, and_5_out);
  and and_10 (and_10_out, or_1_out, and_6_out);
  and and_11 (and_11_out, or_1_out, or_2_out, and_7_out);
  and and_12 (and_12_out, or_1_out, or_2_out, and_8_out);
  and and_13 (and_13_out, or_1_out, or_2_out, or_3_out, and_1_out);
  and and_14 (and_14_out, or_1_out, or_2_out, or_3_out, and_2_out);
  and and_15 (out_11, or_1_out, or_2_out, or_3_out, or_4_out);
  or or_5 (out_9, and_3_out, and_9_out, and_11_out, and_13_out);
  or or_6 (out_10, and_10_out, and_4_out, and_12_out, and_14_out);
endmodule

module Main_CPU_16bit (
);

  wire alu_16_bit_1_positive, alu_16_bit_1_zero, clock_1_out, controlunit_1_alu_add, controlunit_1_alu_and,
       controlunit_1_alu_bmux, controlunit_1_alu_lshift, controlunit_1_alu_rshift, controlunit_1_alu_sub,
       controlunit_1_alu_xor, controlunit_1_ir_write, controlunit_1_mem_write, controlunit_1_pc_load,
       controlunit_1_pc_write, controlunit_1_read_rd_mux, controlunit_1_reg_write,
       controlunit_1_reg_write_src, decoder_1_out0, decoder_1_out1, decoder_1_out2, decoder_1_out3;
  wire [1:0] controlunit_1_mem_addr_mux, counter_2_q;
  wire [3:0] multiplexer_2_out;
  wire [7:0] counter_1_q, undriven, undriven_2, undriven_3;
  wire [15:0] alu_16_bit_1_out1, IR_q, multiplexer_3_out, ram_1_dout, register_1_q, register_file_1_rs_data,
       register_file_1_rt_data;

  Counter counter_1 (
    .load(controlunit_1_pc_load), .D(IR_q[7:0]), .count(controlunit_1_pc_write), .Q(counter_1_q),
    .clk(clock_1_out));  // open: carry, up, clr
  Clock clock_1 (.out(clock_1_out));
  Counter #(.max('h3), .width(2)) counter_2 (
    .Q(counter_2_q), .clk(clock_1_out));  // open: load, D, count, carry, up, clr
  Decoder #(.select(2)) decoder_1 (
    .out0(decoder_1_out0), .out1(decoder_1_out1), .out2(decoder_1_out2), .out3(decoder_1_out3),
    .sel(counter_2_q));  // open: en
  Multiplexer #(.select(2), .width(8)) multiplexer_1 (
    .in0(undriven), .in1(undriven_3), .in2(undriven_2));  // open: in3, out, sel
  RAM #(.dataWidth(16), .\type ("nonvolatile")) ram_1 (
    .addr(counter_1_q), .we(controlunit_1_mem_write), .oe(1'b1), .clk(clock_1_out), .dout(ram_1_dout));  // open: din
  ControlUnit controlunit_1 (
    .opcode(IR_q[15:12]), .Fetch(decoder_1_out0), .Fetch_Write(decoder_1_out1), .Execute(decoder_1_out2),
    .Execute_WRITE(decoder_1_out3), .ALU_Zero(alu_16_bit_1_zero), .ALU_Positive(alu_16_bit_1_positive),
    .ALU_ADD(controlunit_1_alu_add), .ALU_SUB(controlunit_1_alu_sub), .ALU_AND(controlunit_1_alu_and),
    .ALU_XOR(controlunit_1_alu_xor), .ALU_LSHIFT(controlunit_1_alu_lshift),
    .ALU_RSHIFT(controlunit_1_alu_rshift), .ALU_BMux(controlunit_1_alu_bmux),
    .Mem_Addr_Mux(controlunit_1_mem_addr_mux), .Mem_Write(controlunit_1_mem_write),
    .Reg_Write(controlunit_1_reg_write), .Reg_Write_SRC(controlunit_1_reg_write_src),
    .Read_Rd_Mux(controlunit_1_read_rd_mux), .PC_Write(controlunit_1_pc_write),
    .PC_Load(controlunit_1_pc_load), .IR_Write(controlunit_1_ir_write));
  Register #(.width(16)) IR (.D(ram_1_dout), .en(controlunit_1_ir_write), .clk(clock_1_out), .Q(IR_q));  // open: clr
  // Probe on IR_q[3:0]
  // Probe on IR_q[7:4]
  Multiplexer #(.width(4)) multiplexer_2 (
    .in0(IR_q[3:0]), .in1(IR_q[11:8]), .out(multiplexer_2_out), .sel(controlunit_1_read_rd_mux));
  // Probe on IR_q[7:4]
  // Probe on multiplexer_2_out
  Register_file register_file_1 (
    .rs_addr(IR_q[7:4]), .rt_addr(multiplexer_2_out), .rd_addr(IR_q[11:8]), .Write_Data(register_1_q),
    .Reg_Write(controlunit_1_reg_write), .Read_Rd_Mux(controlunit_1_read_rd_mux), .Clock(clock_1_out),
    .rs_data(register_file_1_rs_data), .rt_data(register_file_1_rt_data));
  // Probe on register_file_1_rt_data
  // Probe on register_file_1_rs_data
  Multiplexer #(.width(16)) multiplexer_3 (
    .in0(register_file_1_rt_data), .in1({IR_q[7:0], IR_q[7:0]}), .out(multiplexer_3_out),
    .sel(controlunit_1_alu_bmux));
  // Probe on multiplexer_3_out
  ALU_16_bit alu_16_bit_1 (
    .A(register_file_1_rs_data), .B(multiplexer_3_out), .ADD(controlunit_1_alu_add),
    .AND1(controlunit_1_alu_and), .XOR1(controlunit_1_alu_xor), .SUB(controlunit_1_alu_sub),
    .LSHIFT(controlunit_1_alu_lshift), .RSHIFT(controlunit_1_alu_rshift), .Zero(alu_16_bit_1_zero),
    .OUT1(alu_16_bit_1_out1), .Positive(alu_16_bit_1_positive));
  // Probe on alu_16_bit_1_out1
  Register #(.width(16)) register_1 (
    .D(alu_16_bit_1_out1), .en(1'b1), .clk(clock_1_out), .Q(register_1_q));  // open: clr
endmodule

module ControlUnit (
  input  [3:0] opcode,
  input  Fetch,
  input  Fetch_Write,
  input  Execute,
  input  Execute_WRITE,
  input  ALU_Zero,
  input  ALU_Positive,
  output ALU_ADD,
  output ALU_SUB,
  output ALU_AND,
  output ALU_XOR,
  output ALU_LSHIFT,
  output ALU_RSHIFT,
  output ALU_BMux,
  output [1:0] Mem_Addr_Mux,
  output Mem_Write,
  output Reg_Write,
  output Reg_Write_SRC,
  output Read_Rd_Mux,
  output PC_Write,
  output PC_Load,
  output IR_Write
);

  wire and_4_out, and_5_out, and_6_out, and_8_out, and_11_out, and_14_out, and_15_out, and_18_out,
       and_19_out, and_20_out, decoder_1_out1, decoder_1_out2, decoder_1_out3, decoder_1_out4,
       decoder_1_out5, decoder_1_out6, decoder_1_out7, decoder_1_out8, decoder_1_out9, decoder_1_out12,
       decoder_1_out13;

  Decoder #(.select(4)) decoder_1 (
    .out1(decoder_1_out1), .out2(decoder_1_out2), .out3(decoder_1_out3), .out4(decoder_1_out4),
    .out5(decoder_1_out5), .out6(decoder_1_out6), .out7(decoder_1_out7), .out8(decoder_1_out8),
    .out9(decoder_1_out9), .out12(decoder_1_out12), .out13(decoder_1_out13), .sel(opcode));  // open: out0, out10, out11, out14, out15, en
  and and_1 (ALU_ADD, decoder_1_out1, Execute);
  and and_2 (ALU_AND, decoder_1_out3, Execute);
  and and_3 (ALU_BMux, decoder_1_out7, Execute);
  and and_4 (and_4_out, decoder_1_out8, Execute);
  and and_5 (and_5_out, decoder_1_out12, Execute_WRITE, ALU_Zero);
  and and_6 (and_6_out, decoder_1_out13, Execute_WRITE, ALU_Positive);
  and and_7 (ALU_SUB, decoder_1_out2, Execute);
  and and_8 (and_8_out, decoder_1_out1, Execute_WRITE);
  and and_9 (ALU_XOR, decoder_1_out4, Execute);
  and and_10 (ALU_LSHIFT, decoder_1_out5, Execute);
  and and_11 (and_11_out, decoder_1_out7, Execute_WRITE);
  and and_12 (Reg_Write_SRC, decoder_1_out8, Execute_WRITE);
  and and_13 (Read_Rd_Mux, decoder_1_out9, Execute);
  and and_14 (and_14_out, decoder_1_out2, Execute_WRITE);
  and and_15 (and_15_out, decoder_1_out3, Execute_WRITE);
  and and_16 (ALU_RSHIFT, decoder_1_out6, Execute);
  and and_17 (Mem_Write, decoder_1_out9, Execute_WRITE);
  and and_18 (and_18_out, decoder_1_out4, Execute_WRITE);
  and and_19 (and_19_out, decoder_1_out5, Execute_WRITE);
  and and_20 (and_20_out, decoder_1_out6, Execute_WRITE);
  or or_1 (Reg_Write, and_11_out, and_15_out, and_8_out, and_18_out, and_19_out, and_14_out, and_20_out, Reg_Write_SRC);
  or or_2 (Mem_Addr_Mux[0], and_4_out, Read_Rd_Mux);
  or or_3 (PC_Load, and_6_out, and_5_out);

  assign IR_Write = Fetch_Write;
  assign PC_Write = Fetch_Write;
endmodule

module ControlUnit_V2 (
  input  [3:0] opcode,
  input  Fetch,
  input  Fetch_Write,
  input  Execute,
  input  Execute_WRITE,
  input  ALU_Zero,
  input  ALU_Positive,
  output HALT,
  output ALU_ADD,
  output ALU_SUB,
  output ALU_AND,
  output ALU_XOR,
  output ALU_LSHIFT,
  output ALU_RSHIFT,
  output ALU_BMux,
  output [1:0] Mem_Addr_Mux,
  output Mem_Write,
  output Reg_Write,
  output [1:0] Reg_Write_SRC,
  output Read_Rd_Mux,
  output PC_Write,
  output PC_Load,
  output IR_Write,
  output PC_MUX
);

  wire and_2_out, and_8_out, and_9_out, and_10_out, and_11_out, and_12_out, and_13_out, and_14_out,
       and_15_out, and_16_out, and_17_out, and_18_out, and_19_out, and_20_out, and_21_out, and_22_out,
       and_23_out, and_24_out, and_25_out, and_26_out, and_27_out, and_28_out, and_29_out, and_30_out,
       and_31_out, and_32_out, decoder_1_out0, decoder_1_out1, decoder_1_out2, decoder_1_out3,
       decoder_1_out4, decoder_1_out5, decoder_1_out6, decoder_1_out7, decoder_1_out8, decoder_1_out9,
       decoder_1_out10, decoder_1_out11, decoder_1_out12, decoder_1_out13, decoder_1_out14, decoder_1_out15,
       not_1_out, or_1_out;

  Decoder #(.select(4)) decoder_1 (
    .out0(decoder_1_out0), .out1(decoder_1_out1), .out2(decoder_1_out2), .out3(decoder_1_out3),
    .out4(decoder_1_out4), .out5(decoder_1_out5), .out6(decoder_1_out6), .out7(decoder_1_out7),
    .out8(decoder_1_out8), .out9(decoder_1_out9), .out10(decoder_1_out10), .out11(decoder_1_out11),
    .out12(decoder_1_out12), .out13(decoder_1_out13), .out14(decoder_1_out14), .out15(decoder_1_out15),
    .sel(opcode));  // open: en
  and and_1 (HALT, decoder_1_out0, Execute);
  and and_2 (and_2_out, decoder_1_out1, Execute);
  and and_3 (ALU_SUB, decoder_1_out2, Execute);
  and and_4 (ALU_AND, decoder_1_out3, Execute);
  and and_5 (ALU_XOR, decoder_1_out4, Execute);
  and and_6 (ALU_LSHIFT, decoder_1_out5, Execute);
  and and_7 (ALU_RSHIFT, decoder_1_out6, Execute);
  and and_8 (and_8_out, decoder_1_out7, Execute);
  and and_9 (and_9_out, decoder_1_out8, Execute);
  and and_10 (and_10_out, decoder_1_out9, Execute);
  and and_11 (and_11_out, decoder_1_out10, Execute);
  and and_12 (and_12_out, decoder_1_out11, Execute);
  and and_13 (and_13_out, decoder_1_out12, Execute);
  and and_14 (and_14_out, decoder_1_out13, Execute);
  and and_15 (and_15_out, decoder_1_out14, Execute);
  and and_16 (and_16_out, decoder_1_out15, Execute);
  and and_17 (and_17_out, decoder_1_out1, Execute_WRITE);
  and and_18 (and_18_out, decoder_1_out2, Execute_WRITE);
  and and_19 (and_19_out, decoder_1_out3, Execute_WRITE);
  and and_20 (and_20_out, decoder_1_out4, Execute_WRITE);
  and and_21 (and_21_out, decoder_1_out5, Execute_WRITE);
  and and_22 (and_22_out, decoder_1_out6, Execute_WRITE);
  and and_23 (and_23_out, decoder_1_out7, Execute_WRITE);
  and and_24 (and_24_out, decoder_1_out8, Execute_WRITE);
  and and_25 (and_25_out, decoder_1_out9, Execute_WRITE);
  and and_26 (and_26_out, decoder_1_out10, Execute_WRITE);
  and and_27 (and_27_out, decoder_1_out11, Execute_WRITE);
  and and_28 (and_28_out, decoder_1_out12, Execute_WRITE);
  and and_29 (and_29_out, decoder_1_out13, Execute_WRITE);
  and and_30 (and_30_out, decoder_1_out14, Execute_WRITE);
  and and_31 (and_31_out, decoder_1_out15, Execute_WRITE);
  or or_1 (or_1_out, decoder_1_out10, decoder_1_out11);
  or or_2 (ALU_BMux, and_9_out, and_8_out, and_10_out);
  or or_3 (Mem_Write, and_25_out, and_27_out);
  and and_32 (and_32_out, and_29_out, ALU_Zero);
  or or_4 (PC_Load, and_15_out, and_28_out, and_30_out, and_31_out, and_32_out, and_13_out);
  or or_5 (Mem_Addr_Mux[0], and_27_out, and_24_out, and_9_out, and_10_out, and_30_out, and_12_out, and_11_out, and_25_out, and_15_out);
  or or_6 (Read_Rd_Mux, and_25_out, and_10_out, and_12_out, and_13_out, and_14_out, and_15_out, and_16_out, and_30_out);
  or or_7 (Reg_Write_SRC[1], and_31_out, and_16_out);
  or or_8 (ALU_ADD, and_2_out, and_15_out, and_30_out, and_8_out);
  and and_33 (Mem_Addr_Mux[1], or_1_out, not_1_out);
  or or_9 (Reg_Write, and_16_out, and_17_out, ALU_SUB, and_19_out, and_20_out, and_21_out, and_22_out, and_23_out, and_24_out, and_8_out, and_31_out, and_26_out);
  not not_1 (not_1_out, Fetch_Write);
  or or_10 (Reg_Write_SRC[0], and_24_out, and_11_out, and_31_out, and_9_out, and_26_out);
  or or_11 (PC_MUX, and_24_out, and_30_out);
  or or_12 (PC_Write, PC_Load, Fetch_Write);

  assign IR_Write = Fetch_Write;
endmodule

module MainCPU16Bit_V2 (
);

  wire alu_16_bit_1_positive, alu_16_bit_1_zero, and_1_out, clock_1_out, controlunit_v2_1_alu_add,
       controlunit_v2_1_alu_and, controlunit_v2_1_alu_bmux, controlunit_v2_1_alu_lshift,
       controlunit_v2_1_alu_rshift, controlunit_v2_1_alu_sub, controlunit_v2_1_alu_xor,
       controlunit_v2_1_halt, controlunit_v2_1_ir_write, controlunit_v2_1_mem_write,
       controlunit_v2_1_pc_load, controlunit_v2_1_pc_mux, controlunit_v2_1_pc_write,
       controlunit_v2_1_read_rd_mux, controlunit_v2_1_reg_write, decoder_1_out0, decoder_1_out1,
       decoder_1_out2, decoder_1_out3, not_1_out, not_2_out, undriven_2;
  wire [1:0] controlunit_v2_1_mem_addr_mux, controlunit_v2_1_reg_write_src, counter_1_q;
  wire [3:0] register_4_q_2;
  wire [7:0] adder_1_out, counter_2_q, multiplexer_1_out, multiplexer_2_out, multiplexer_3_out,
       multiplexer_4_out, multiplexer_4_out_2, register_1_q, register_2_q, register_4_q, subtractor_1_out,
       undriven;
  wire [15:0] alu_16_bit_1_out1, multiplexer_5_out, ram_1_dout, register_3_q, register_5_q,
       register_file_1_rs_data, register_file_1_rt_data;
  wire [15:12] register_4_q_3;

  Register register_1 (.D(register_4_q), .en(decoder_1_out0), .clk(and_1_out), .Q(register_1_q));  // open: clr
  Clock clock_1 (.out(clock_1_out));
  not not_1 (not_1_out, controlunit_v2_1_halt);
  Multiplexer #(.width(8)) multiplexer_1 (
    .in0(register_4_q), .in1(register_1_q), .out(multiplexer_1_out), .sel(controlunit_v2_1_pc_mux));
  Multiplexer #(.width(8)) multiplexer_2 (
    .in0(adder_1_out), .in1(multiplexer_1_out), .out(multiplexer_2_out), .sel(controlunit_v2_1_pc_load));
  and and_1 (and_1_out, not_1_out, clock_1_out);
  Counter #(.max('h3), .trigger("falling"), .width(2)) counter_1 (
    .Q(counter_1_q), .clk(and_1_out));  // open: load, D, count, carry, up, clr
  Register register_2 (
    .D(multiplexer_2_out), .en(controlunit_v2_1_pc_write), .clk(and_1_out), .Q(register_2_q));  // open: clr
  // Probe on multiplexer_2_out
  // Probe on controlunit_v2_1_pc_load
  // Probe on register_2_q
  Decoder #(.select(2)) decoder_1 (
    .out0(decoder_1_out0), .out1(decoder_1_out1), .out2(decoder_1_out2), .out3(decoder_1_out3),
    .sel(counter_1_q));  // open: en
  ControlUnit_V2 controlunit_v2_1 (
    .opcode(register_4_q_3), .Fetch(decoder_1_out0), .Fetch_Write(decoder_1_out1), .Execute(decoder_1_out2),
    .Execute_WRITE(decoder_1_out3), .ALU_Zero(alu_16_bit_1_zero), .ALU_Positive(alu_16_bit_1_positive),
    .HALT(controlunit_v2_1_halt), .ALU_ADD(controlunit_v2_1_alu_add), .ALU_SUB(controlunit_v2_1_alu_sub),
    .ALU_AND(controlunit_v2_1_alu_and), .ALU_XOR(controlunit_v2_1_alu_xor),
    .ALU_LSHIFT(controlunit_v2_1_alu_lshift), .ALU_RSHIFT(controlunit_v2_1_alu_rshift),
    .ALU_BMux(controlunit_v2_1_alu_bmux), .Mem_Addr_Mux(controlunit_v2_1_mem_addr_mux),
    .Mem_Write(controlunit_v2_1_mem_write), .Reg_Write(controlunit_v2_1_reg_write),
    .Reg_Write_SRC(controlunit_v2_1_reg_write_src), .Read_Rd_Mux(controlunit_v2_1_read_rd_mux),
    .PC_Write(controlunit_v2_1_pc_write), .PC_Load(controlunit_v2_1_pc_load),
    .IR_Write(controlunit_v2_1_ir_write), .PC_MUX(controlunit_v2_1_pc_mux));
  // Probe on adder_1_out
  Adder adder_1 (.a(register_2_q), .b(8'h1), .out(adder_1_out));  // open: cin, cout
  // Probe on controlunit_v2_1_pc_write
  // Probe on controlunit_v2_1_pc_load
  Subtractor subtractor_1 (.a(adder_1_out), .b(8'h1), .out(subtractor_1_out));  // open: bin, bout
  Multiplexer #(.select(2), .width(8)) multiplexer_3 (
    .in0(subtractor_1_out), .in1(register_4_q), .in2(register_file_1_rt_data[7:0]), .in3(multiplexer_4_out),
    .out(multiplexer_3_out), .sel(controlunit_v2_1_mem_addr_mux));
  Counter #(.trigger("falling")) counter_2 (
    .load(undriven_2), .D(register_4_q), .Q(counter_2_q), .clk(and_1_out));  // open: count, carry, up, clr
  Register #(.width(16)) register_3 (
    .D(register_file_1_rs_data), .en(decoder_1_out0), .clk(and_1_out), .Q(register_3_q));  // open: clr
  RAM #(.dataWidth(16), .\type ("nonvolatile")) ram_1 (
    .addr(multiplexer_3_out), .we(controlunit_v2_1_mem_write), .oe(not_2_out), .clk(and_1_out),
    .din(register_3_q), .dout(ram_1_dout));
  not not_2 (not_2_out, controlunit_v2_1_mem_write);
  // Probe on register_4_q_2
  // Probe on multiplexer_5_out
  // Probe on register_file_1_rt_data
  Register_file register_file_1 (
    .rs_addr(register_4_q[7:4]), .rt_addr(register_4_q[3:0]), .rd_addr(register_4_q_2),
    .Write_Data(multiplexer_5_out), .Reg_Write(controlunit_v2_1_reg_write),
    .Read_Rd_Mux(controlunit_v2_1_read_rd_mux), .Clock(and_1_out), .rs_data(register_file_1_rs_data),
    .rt_data(register_file_1_rt_data));
  // Probe on register_file_1_rs_data
  Multiplexer #(.width(16)) multiplexer_4 (
    .in0(register_file_1_rt_data), .in1({{8{1'b0}}, register_4_q}),
    .out({multiplexer_4_out_2, multiplexer_4_out}), .sel(controlunit_v2_1_alu_bmux));
  // Probe on ram_1_dout
  // Probe on {multiplexer_4_out_2, multiplexer_4_out}
  Register #(.trigger("falling"), .width(16)) register_4 (
    .D(ram_1_dout), .en(controlunit_v2_1_ir_write), .clk(and_1_out),
    .Q({register_4_q_3, register_4_q_2, register_4_q}));  // open: clr
  ALU_16_bit alu_16_bit_1 (
    .A({multiplexer_4_out_2, multiplexer_4_out}), .B(register_file_1_rs_data),
    .ADD(controlunit_v2_1_alu_add), .AND1(controlunit_v2_1_alu_and), .XOR1(controlunit_v2_1_alu_xor),
    .SUB(controlunit_v2_1_alu_sub), .LSHIFT(controlunit_v2_1_alu_lshift),
    .RSHIFT(controlunit_v2_1_alu_rshift), .Zero(alu_16_bit_1_zero), .OUT1(alu_16_bit_1_out1),
    .Positive(alu_16_bit_1_positive));
  // Probe on register_4_q
  Register #(.trigger("falling"), .width(16)) register_5 (
    .D(alu_16_bit_1_out1), .en(1'b1), .clk(and_1_out), .Q(register_5_q));  // open: clr
  // Probe on register_5_q
  Multiplexer #(.select(2), .width(16)) multiplexer_5 (
    .in0(register_5_q), .in1(ram_1_dout), .in2({adder_1_out, adder_1_out}), .in3({{8{1'b0}}, undriven}),
    .out(multiplexer_5_out), .sel(controlunit_v2_1_reg_write_src));
  // Probe on register_4_q
  // Probe on controlunit_v2_1_reg_write_src
  // Probe on {{8{1'b0}}, undriven}
  Hex_Digit_Display hex_digit_display_1 (.value(register_5_q[15:12]));  // open: dp
  Hex_Digit_Display hex_digit_display_2 (.value(register_5_q[11:8]));  // open: dp
  Hex_Digit_Display hex_digit_display_3 (.value(register_5_q[7:4]));  // open: dp
  Hex_Digit_Display hex_digit_display_4 (.value(register_5_q[3:0]));  // open: dp
endmodule

module sub_tester (
  input  [15:0] A,
  input  [15:0] B,
  input  SUB,
  output [15:0] out_4
);

  wire [15:0] xor_1_out;

  assign xor_1_out = {16{SUB}} ^ B;  // XOR_Gate xor_1, 16 bits wide
  fulladder fulladder_1 (.CIN(SUB), .A(A), .B(xor_1_out), .OUT1(out_4));
endmodule

module fulladder (
  input  CIN,
  input  [15:0] A,
  input  [15:0] B,
  output [15:0] OUT1
);

  wire full_adder_majandodd_1_cout, full_adder_majandodd_2_cout, full_adder_majandodd_3_cout,
       full_adder_majandodd_4_cout, full_adder_majandodd_5_cout, full_adder_majandodd_6_cout,
       full_adder_majandodd_7_cout, full_adder_majandodd_8_cout, full_adder_majandodd_9_cout,
       full_adder_majandodd_10_cout, full_adder_majandodd_11_cout, full_adder_majandodd_12_cout,
       full_adder_majandodd_13_cout, full_adder_majandodd_14_cout, full_adder_majandodd_15_cout;

  Full_adder_majANDodd full_adder_majandodd_1 (
    .A(A[0]), .B(B[0]), .Carry(CIN), .Sum(OUT1[0]), .Cout(full_adder_majandodd_1_cout));
  Full_adder_majANDodd full_adder_majandodd_2 (
    .A(A[1]), .B(B[1]), .Carry(full_adder_majandodd_1_cout), .Sum(OUT1[1]), .Cout(full_adder_majandodd_2_cout));
  Full_adder_majANDodd full_adder_majandodd_3 (
    .A(A[2]), .B(B[2]), .Carry(full_adder_majandodd_2_cout), .Sum(OUT1[2]), .Cout(full_adder_majandodd_3_cout));
  Full_adder_majANDodd full_adder_majandodd_4 (
    .A(A[3]), .B(B[3]), .Carry(full_adder_majandodd_3_cout), .Sum(OUT1[3]), .Cout(full_adder_majandodd_4_cout));
  Full_adder_majANDodd full_adder_majandodd_5 (
    .A(A[4]), .B(B[4]), .Carry(full_adder_majandodd_4_cout), .Sum(OUT1[4]), .Cout(full_adder_majandodd_5_cout));
  Full_adder_majANDodd full_adder_majandodd_6 (
    .A(A[5]), .B(B[5]), .Carry(full_adder_majandodd_5_cout), .Sum(OUT1[5]), .Cout(full_adder_majandodd_6_cout));
  Full_adder_majANDodd full_adder_majandodd_7 (
    .A(A[6]), .B(B[6]), .Carry(full_adder_majandodd_6_cout), .Sum(OUT1[6]), .Cout(full_adder_majandodd_7_cout));
  Full_adder_majANDodd full_adder_majandodd_8 (
    .A(A[7]), .B(B[7]), .Carry(full_adder_majandodd_7_cout), .Sum(OUT1[7]), .Cout(full_adder_majandodd_8_cout));
  Full_adder_majANDodd full_adder_majandodd_9 (
    .A(A[8]), .B(B[8]), .Carry(full_adder_majandodd_8_cout), .Sum(OUT1[8]), .Cout(full_adder_majandodd_9_cout));
  Full_adder_majANDodd full_adder_majandodd_10 (
    .A(A[9]), .B(B[9]), .Carry(full_adder_majandodd_9_cout), .Sum(OUT1[9]),
    .Cout(full_adder_majandodd_10_cout));
  Full_adder_majANDodd full_adder_majandodd_11 (
    .A(A[10]), .B(B[10]), .Carry(full_adder_majandodd_10_cout), .Sum(OUT1[10]),
    .Cout(full_adder_majandodd_11_cout));
  Full_adder_majANDodd full_adder_majandodd_12 (
    .A(A[11]), .B(B[11]), .Carry(full_adder_majandodd_11_cout), .Sum(OUT1[11]),
    .Cout(full_adder_majandodd_12_cout));
  Full_adder_majANDodd full_adder_majandodd_13 (
    .A(A[12]), .B(B[12]), .Carry(full_adder_majandodd_12_cout), .Sum(OUT1[12]),
    .Cout(full_adder_majandodd_13_cout));
  Full_adder_majANDodd full_adder_majandodd_14 (
    .A(A[13]), .B(B[13]), .Carry(full_adder_majandodd_13_cout), .Sum(OUT1[13]),
    .Cout(full_adder_majandodd_14_cout));
  Full_adder_majANDodd full_adder_majandodd_15 (
    .A(A[14]), .B(B[14]), .Carry(full_adder_majandodd_14_cout), .Sum(OUT1[14]),
    .Cout(full_adder_majandodd_15_cout));
  Full_adder_majANDodd full_adder_majandodd_16 (
    .A(A[15]), .B(B[15]), .Carry(full_adder_majandodd_15_cout), .Sum(OUT1[15]));  // open: Cout
endmodule
